// Digital circuit lm8.dig as structural Verilog
module lm8 (
  input  Clock
);

  wire add_3_c_o, add_4_c_o, and_1_out, ClearScreen, comparator_1_gt, comparator_2_lt, comparator_3_lt,
       comparator_4_lt, comparator_5_lt, comparator_6_lt, CondEn, demultiplexer_1_out_0,
       demultiplexer_1_out_1, demultiplexer_1_out_2, demultiplexer_1_out_3, demultiplexer_1_out_4,
       demultiplexer_1_out_5, demultiplexer_2_out_0, demultiplexer_2_out_1, demultiplexer_2_out_2,
       demultiplexer_2_out_3, demultiplexer_3_out_0, demultiplexer_3_out_2, demultiplexer_3_out_3,
       demultiplexer_3_out_4, demultiplexer_3_out_5, demultiplexer_3_out_6, demultiplexer_3_out_7,
       demultiplexer_3_out_10, demultiplexer_3_out_11, demultiplexer_3_out_12, demultiplexer_3_out_13,
       demultiplexer_3_out_14, demultiplexer_3_out_15, demultiplexer_3_out_16, demultiplexer_3_out_17,
       demultiplexer_3_out_18, demultiplexer_3_out_19, demultiplexer_3_out_30, demultiplexer_3_out_31,
       demultiplexer_3_out_108, demultiplexer_3_out_109, demultiplexer_3_out_110, demultiplexer_3_out_111,
       demultiplexer_3_out_112, demultiplexer_3_out_113, DrawPixel, DrawSprite, Halt, Halted, IncPC, IncSP,
       IngestInstr, InstrDone, KEY0, KEY1, MemWrite, multiplexer_1_out, multiplexer_2_out, nor_1_out,
       not_1_out, not_2_out, or_1_out, or_2_out, or_3_out, or_4_out, or_6_out, PortWrite,
       priorityencoder_1_any, sub_2_c_o, sub_3_c_o, Timer0, Timer1, Write, WriteF, WritePC, WriteSP,
       xnor_1_out, xor_2_out;
  wire [0:0] comparator_8_gt, comparator_9_gt, comparator_10_gt;
  wire [1:0] AddrMode, and_3_out, Microcode_d, multiplexer_14_out, Operation, RegCondSel;
  wire [2:0] WriteSel;
  wire [2:2] add_7_c_o, sub_5_c_o;
  wire [3:0] add_1_s, F, Instr_State_q, Mode, multiplexer_4_out, multiplexer_11_out, multiplexer_21_out,
       NewF, priorityencoder_1_num, ReadSel, sub_1_s, WASD;
  wire [3:2] multiplexer_13_out;
  wire [7:0] A, add_3_s, add_4_s, add_6_s, add_7_s, and_2_out, B, barrelshifter_1_out, barrelshifter_2_out,
       barrelshifter_3_out, C0, C1, Data, GraphicsX, GraphicsY, H, Instr_q, L, Memory, Memory_d1, Memory_d2,
       MemoryGfx, multiplexer_5_out, multiplexer_8_out, multiplexer_15_out, multiplexer_17_out, Operand,
       or_5_out, PortIn, prng_1_r, Program_d1, Program_d2, SP, sub_2_s, sub_3_s, sub_4_s, sub_5_s, sub_6_s,
       sub_7_s, sub_8_s, xor_1_out;
  wire [7:2] multiplexer_9_out;
  wire [8:0] add_2_s;
  wire [9:0] and_4_out, and_5_out, and_6_out, barrelshifter_4_out, barrelshifter_5_out, barrelshifter_6_out,
       barrelshifter_7_out, LEDs, not_3_out, or_7_out, Switches;
  wire [11:0] mul_1_mul;
  wire [15:0] add_5_s, add_8_s, bitextender_1_out, multiplexer_3_out, multiplexer_16_out, multiplexer_18_out,
       PC;
  wire [23:0] HEX;

  LED led_1 (.in(LEDs[9]));
  Multiplexer #(.Selector_Bits(2)) multiplexer_1 (
    .sel(RegCondSel), .in_0(F[3]), .in_1(F[2]), .in_2(F[1]), .in_3(F[0]), .out(multiplexer_1_out));
  Comparator #(.Bits(8)) comparator_1 (.a(Data), .b({8{1'b0}}), .gt(comparator_1_gt));  // open: eq, lt
  Comparator #(.Bits(8)) comparator_2 (.a(Data), .b({8{1'b1}}), .lt(comparator_2_lt));  // open: gt, eq
  Demultiplexer #(.Selector_Bits(3)) demultiplexer_1 (
    .sel(WriteSel), .in(Write), .out_0(demultiplexer_1_out_0), .out_1(demultiplexer_1_out_1),
    .out_2(demultiplexer_1_out_2), .out_3(demultiplexer_1_out_3), .out_4(demultiplexer_1_out_4),
    .out_5(demultiplexer_1_out_5), .out_6(MemWrite), .out_7(PortWrite));
  LED led_2 (.in(LEDs[8]));
  LED led_3 (.in(LEDs[7]));
  not not_1 (not_1_out, multiplexer_1_out);
  LED led_4 (.in(LEDs[6]));
  LED led_5 (.in(LEDs[5]));
  Multiplexer #(.Selector_Bits(2)) multiplexer_2 (
    .sel(Mode[1:0]), .in_0(multiplexer_1_out), .in_1(not_1_out), .in_2(comparator_1_gt),
    .in_3(comparator_2_lt), .out(multiplexer_2_out));
  Demultiplexer #(.Selector_Bits(2)) demultiplexer_2 (
    .sel(RegCondSel), .in(demultiplexer_1_out_1), .out_0(demultiplexer_2_out_0),
    .out_1(demultiplexer_2_out_1), .out_2(demultiplexer_2_out_2), .out_3(demultiplexer_2_out_3));
  Multiplexer #(.Bits(16), .Selector_Bits(2)) multiplexer_3 (
    .sel(AddrMode), .in_0(PC), .in_1({{8{1'b1}}, SP}), .in_2({H, L}), .in_3({C0, C1}), .out(multiplexer_3_out));
  LED led_6 (.in(LEDs[4]));
  LED led_7 (.in(LEDs[3]));
  and and_1 (and_1_out, multiplexer_2_out, CondEn);
  or or_1 (or_1_out, demultiplexer_1_out_0, demultiplexer_2_out_0);
  or or_2 (or_2_out, demultiplexer_2_out_2, demultiplexer_1_out_2);
  or or_3 (or_3_out, demultiplexer_2_out_3, demultiplexer_1_out_3);
  LED led_8 (.in(LEDs[2]));
  LED led_9 (.in(LEDs[1]));
  Seven_Seg_Hex seven_seg_hex_1 (.d(HEX[23:20]), .dp(1'b0));
  LED led_10 (.in(LEDs[0]));
  nor nor_1 (nor_1_out, Halted, 1'b0);
  or or_4 (or_4_out, InstrDone, and_1_out);
  Register #(.Bits(8)) u_A (.D(Data), .C(Clock), .en(or_1_out), .Q(A));
  Register #(.Bits(8)) u_B (.D(Data), .C(Clock), .en(demultiplexer_2_out_1), .Q(B));
  Register #(.Bits(8)) u_H (.D(Data), .C(Clock), .en(or_2_out), .Q(H));
  Register #(.Bits(8)) u_L (.D(Data), .C(Clock), .en(or_3_out), .Q(L));
  Register #(.Bits(8)) u_C0 (.D(Data), .C(Clock), .en(demultiplexer_1_out_4), .Q(C0));
  Register #(.Bits(8)) u_C1 (.D(Data), .C(Clock), .en(demultiplexer_1_out_5), .Q(C1));
  ROMDualPort #(.AddrBits(15), .Bits(8)) Program (
    .A1(multiplexer_3_out[14:0]), .s1(1'b1), .A2({15{1'b0}}), .s2(1'b1), .D1(Program_d1), .D2(Program_d2));
  RAMDualAccess #(.AddrBits(15), .Bits(8)) u_Memory (
    .str(MemWrite), .C(Clock), .ld(1'b1), .A1(multiplexer_3_out[14:0]), .Din1(Data), .A2({15{1'b0}}),
    .D1(Memory_d1), .D2(Memory_d2));
  Seven_Seg_Hex seven_seg_hex_2 (.d(HEX[19:16]), .dp(1'b0));
  Seven_Seg_Hex seven_seg_hex_3 (.d(HEX[15:12]), .dp(1'b0));
  Register #(.Bits(8)) Instr (.D(Memory), .C(Clock), .en(IngestInstr), .Q(Instr_q));
  Register #(.Bits(4)) Instr_State (.D(multiplexer_4_out), .C(Clock), .en(nor_1_out), .Q(Instr_State_q));
  Multiplexer #(.Bits(4)) multiplexer_4 (.sel(or_4_out), .in_0(add_1_s), .in_1(4'b0000), .out(multiplexer_4_out));
  Seven_Seg_Hex seven_seg_hex_4 (.d(HEX[11:8]), .dp(1'b0));
  Seven_Seg_Hex seven_seg_hex_5 (.d(HEX[7:4]), .dp(1'b0));
  Add #(.Bits(4)) add_1 (.a(4'b0001), .b(Instr_State_q), .c_i(1'b0), .s(add_1_s));  // open: c_o
  Multiplexer #(.Selector_Bits(2), .Bits(8)) multiplexer_5 (
    .sel(RegCondSel), .in_0(A), .in_1(B), .in_2(H), .in_3(L), .out(multiplexer_5_out));
  Multiplexer #(.Bits(8)) multiplexer_6 (
    .sel(multiplexer_3_out[15]), .in_0(Program_d1), .in_1(Memory_d1), .out(Memory));
  Multiplexer #(.Bits(8)) multiplexer_7 (.sel(1'b0), .in_0(Program_d2), .in_1(Memory_d2), .out(MemoryGfx));
  Seven_Seg_Hex seven_seg_hex_6 (.d(HEX[3:0]), .dp(1'b0));
  Multiplexer #(.Bits(8)) multiplexer_8 (.sel(not_2_out), .in_0(Memory), .in_1(Instr_q), .out(multiplexer_8_out));
  Comparator #(.Bits(4)) comparator_3 (.a(Instr_State_q), .b(4'b0010), .lt(comparator_3_lt));  // open: gt, eq
  Comparator #(.Bits(4)) comparator_4 (
    .a(Instr_State_q), .b(4'b0001), .eq(IngestInstr), .lt(comparator_4_lt));  // open: gt
  Multiplexer #(.Bits(8)) multiplexer_9 (
    .sel(comparator_4_lt), .in_0(multiplexer_8_out), .in_1(8'h4), .out({multiplexer_9_out, RegCondSel}));
  not not_2 (not_2_out, comparator_3_lt);
  Button u_KEY1 (.out(KEY1));
  Sub #(.Bits(4)) sub_1 (.a(Instr_State_q), .b(4'b0001), .c_i(1'b0), .s(sub_1_s));  // open: c_o
  Multiplexer #(.Selector_Bits(4), .Bits(8)) multiplexer_10 (
    .sel(ReadSel), .in_0(A), .in_1(multiplexer_5_out), .in_2(H), .in_3(L), .in_4(C0), .in_5(C1),
    .in_6(Memory), .in_7(PC[7:0]), .in_8(PC[15:8]), .in_9(PortIn), .in_10(8'hee), .in_11(8'hee),
    .in_12(8'hee), .in_13(8'hee), .in_14(8'hee), .in_15(8'hee), .out(Operand));
  Button u_KEY0 (.out(KEY0));
  Mul #(.Bits(6)) mul_1 (.a(multiplexer_9_out), .b(6'b001000), .mul(mul_1_mul));
  Multiplexer #(.Bits(4)) multiplexer_11 (
    .sel(comparator_4_lt), .in_0(sub_1_s), .in_1(4'b0000), .out(multiplexer_11_out));
  DipSwitch dipswitch_1 (.out(Switches[8]));
  DipSwitch dipswitch_2 (.out(Switches[9]));
  DipSwitch dipswitch_3 (.out(Switches[4]));
  DipSwitch dipswitch_4 (.out(Switches[5]));
  DipSwitch dipswitch_5 (.out(Switches[6]));
  DipSwitch dipswitch_6 (.out(Switches[7]));
  Add #(.Bits(9)) add_2 (
    .a(mul_1_mul[8:0]), .b({{5{1'b0}}, multiplexer_11_out}), .c_i(1'b0), .s(add_2_s));  // open: c_o
  DipSwitch dipswitch_7 (.out(Switches[3]));
  DipSwitch dipswitch_8 (.out(Switches[2]));
  DipSwitch dipswitch_9 (.out(Switches[1]));
  DipSwitch dipswitch_10 (.out(Switches[0]));
  ROM #(.AddrBits(9), .Bits(24)) Microcode (
    .A(add_2_s), .sel(1'b1),
    .D({InstrDone, WritePC, IncPC, Halt, CondEn, WriteF, Write, IncSP, WriteSP, Mode, WriteSel, ReadSel, Operation, Microcode_d}));
  BarrelShifter #(.Bits(8)) barrelshifter_1 (.in(A), .shift(4'b0001), .out(barrelshifter_1_out));
  BarrelShifter #(.Bits(8), .direction("right")) barrelshifter_2 (.in(A), .shift(4'b0001), .out(barrelshifter_2_out));
  BarrelShifter #(.Bits(8), .barrelShifterMode("arithmetic"), .direction("right")) barrelshifter_3 (
    .in(A), .shift(4'b0001), .out(barrelshifter_3_out));
  Add #(.Bits(8)) add_3 (.a(A), .b(Operand), .c_i(1'b0), .s(add_3_s), .c_o(add_3_c_o));
  Add #(.Bits(8)) add_4 (.a(A), .b(Operand), .c_i(F[2]), .s(add_4_s), .c_o(add_4_c_o));
  Sub #(.Bits(8)) sub_2 (.a(A), .b(Operand), .c_i(1'b0), .s(sub_2_s), .c_o(sub_2_c_o));
  Sub #(.Bits(8)) sub_3 (.a(A), .b(Operand), .c_i(F[2]), .s(sub_3_s), .c_o(sub_3_c_o));
  assign and_2_out = A & Operand;  // And and_2, 8 bits wide
  assign or_5_out = A | Operand;  // Or or_5, 8 bits wide
  assign xor_1_out = A ^ Operand;  // XOr xor_1, 8 bits wide
  Multiplexer #(.Bits(2)) multiplexer_12 (.sel(comparator_4_lt), .in_0(Microcode_d), .in_1(2'b01), .out(AddrMode));
  Comparator #(.Signed("true"), .Bits(8)) comparator_5 (.a(A), .b({8{1'b0}}), .lt(comparator_5_lt));  // open: gt, eq
  Comparator #(.Signed("true"), .Bits(8)) comparator_6 (
    .a(Operand), .b({8{1'b0}}), .lt(comparator_6_lt));  // open: gt, eq
  Button UP (.out(WASD[0]));
  Button DOWN (.out(WASD[1]));
  xnor xnor_1 (xnor_1_out, comparator_5_lt, comparator_6_lt);
  Multiplexer #(.Selector_Bits(4)) multiplexer_13 (
    .sel(Mode), .in_0(add_3_c_o), .in_1(add_4_c_o), .in_2(sub_2_c_o), .in_3(sub_3_c_o), .in_4(F[2]),
    .in_5(F[2]), .in_6(F[2]), .in_7(sub_2_c_o), .in_8(A[7]), .in_9(A[0]), .in_10(A[0]), .in_11(F[2]),
    .in_12(F[2]), .in_13(F[2]), .in_14(F[2]), .in_15(F[2]), .out(multiplexer_13_out[2]));
  Button LEFT (.out(WASD[2]));
  Button RIGHT (.out(WASD[3]));
  and and_3 (and_3_out[0], xor_2_out, xnor_1_out);
  Multiplexer #(.Selector_Bits(4), .Bits(2)) multiplexer_14 (
    .sel(Mode), .in_0(F[1:0]), .in_1(F[1:0]), .in_2(F[1:0]), .in_3(F[1:0]), .in_4(F[1:0]), .in_5(F[1:0]),
    .in_6(F[1:0]), .in_7(F[1:0]), .in_8(and_3_out), .in_9(F[1:0]), .in_10(F[1:0]), .in_11(F[1:0]),
    .in_12(and_3_out), .in_13(and_3_out), .in_14(and_3_out), .in_15(and_3_out), .out(multiplexer_14_out));
  xor xor_2 (xor_2_out, and_3_out[1], comparator_6_lt);
  BitExtender bitextender_1 (.in(Data), .out(bitextender_1_out));
  Comparator #(.Signed("true"), .Bits(8)) comparator_7 (
    .a(Data), .b({8{1'b0}}), .eq(multiplexer_13_out[3]), .lt(and_3_out[1]));  // open: gt
  Register #(.Bits(8)) u_SP (.D(multiplexer_17_out), .C(Clock), .en(WriteSP), .Q(SP));
  Multiplexer #(.Selector_Bits(4), .Bits(8)) multiplexer_15 (
    .sel(Mode), .in_0(add_3_s), .in_1(add_4_s), .in_2(sub_2_s), .in_3(sub_3_s), .in_4(and_2_out),
    .in_5(or_5_out), .in_6(xor_1_out), .in_7(sub_2_s), .in_8(barrelshifter_1_out),
    .in_9(barrelshifter_2_out), .in_10(barrelshifter_3_out), .in_11(8'hee), .in_12(8'hee), .in_13(8'hee),
    .in_14(8'hee), .in_15(8'hee), .out(multiplexer_15_out));
  Add #(.Bits(16)) add_5 (.a(PC), .b(bitextender_1_out), .c_i(1'b0), .s(add_5_s));  // open: c_o
  or or_6 (or_6_out, IngestInstr, IncPC, WritePC);
  Add #(.Bits(8)) add_6 (.a(SP), .b(8'h1), .c_i(1'b0), .s(add_6_s));  // open: c_o
  Sub #(.Bits(8)) sub_4 (.a(SP), .b(8'h1), .c_i(1'b0), .s(sub_4_s));  // open: c_o
  Multiplexer #(.Selector_Bits(2), .Bits(16)) multiplexer_16 (
    .sel(Mode[1:0]), .in_0({H, L}), .in_1({C0, C1}), .in_2(add_5_s), .in_3({16{1'b0}}),
    .out(multiplexer_16_out));
  Multiplexer #(.Bits(8)) multiplexer_17 (.sel(IncSP), .in_0(add_6_s), .in_1(sub_4_s), .out(multiplexer_17_out));
  Add #(.Bits(8)) add_7 (.a(Operand), .b(8'h1), .c_i(1'b0), .s(add_7_s), .c_o(add_7_c_o[2]));
  Sub #(.Bits(8)) sub_5 (.a(Operand), .b(8'h1), .c_i(1'b0), .s(sub_5_s), .c_o(sub_5_c_o[2]));
  Register #(.Bits(16)) u_PC (.D(multiplexer_18_out), .C(Clock), .en(or_6_out), .Q(PC));
  Multiplexer #(.Bits(16)) multiplexer_18 (
    .sel(WritePC), .in_0(add_8_s), .in_1(multiplexer_16_out), .out(multiplexer_18_out));
  Add #(.Bits(16)) add_8 (.a(16'h1), .b(PC), .c_i(1'b0), .s(add_8_s));  // open: c_o
  Register #(.Bits(4)) u_F (.D(NewF), .C(Clock), .en(WriteF), .Q(F));
  Register u_Halted (.D(1'b1), .C(Clock), .en(Halt), .Q(Halted));
  Multiplexer #(.Selector_Bits(2), .Bits(4)) multiplexer_19 (
    .sel(Operation), .in_0({multiplexer_13_out, multiplexer_14_out}), .in_1({multiplexer_13_out[3], F[2:0]}),
    .in_2({multiplexer_13_out[3], add_7_c_o[2], F[1:0]}),
    .in_3({multiplexer_13_out[3], sub_5_c_o[2], F[1:0]}), .out(NewF));
  Multiplexer #(.Selector_Bits(2), .Bits(8)) multiplexer_20 (
    .sel(Operation), .in_0(multiplexer_15_out), .in_1(Operand), .in_2(add_7_s), .in_3(sub_5_s), .out(Data));
  Demultiplexer #(.Selector_Bits(7)) demultiplexer_3 (
    .sel(C0[6:0]), .in(PortWrite), .out_0(demultiplexer_3_out_0), .out_2(demultiplexer_3_out_2),
    .out_3(demultiplexer_3_out_3), .out_4(demultiplexer_3_out_4), .out_5(demultiplexer_3_out_5),
    .out_6(demultiplexer_3_out_6), .out_7(demultiplexer_3_out_7), .out_10(demultiplexer_3_out_10),
    .out_11(demultiplexer_3_out_11), .out_12(demultiplexer_3_out_12), .out_13(demultiplexer_3_out_13),
    .out_14(demultiplexer_3_out_14), .out_15(demultiplexer_3_out_15), .out_16(demultiplexer_3_out_16),
    .out_17(demultiplexer_3_out_17), .out_18(demultiplexer_3_out_18), .out_19(demultiplexer_3_out_19),
    .out_30(demultiplexer_3_out_30), .out_31(demultiplexer_3_out_31), .out_32(DrawPixel),
    .out_33(DrawSprite), .out_34(ClearScreen), .out_108(demultiplexer_3_out_108),
    .out_109(demultiplexer_3_out_109), .out_110(demultiplexer_3_out_110), .out_111(demultiplexer_3_out_111),
    .out_112(demultiplexer_3_out_112), .out_113(demultiplexer_3_out_113));  // open: out_1, out_8, out_9, out_20, out_21, out_22, out_23, out_24, out_25, out_26, out_27, out_28, out_29, out_35, out_36, out_37, out_38, out_39, out_40, out_41, out_42, out_43, out_44, out_45, out_46, out_47, out_48, out_49, out_50, out_51, out_52, out_53, out_54, out_55, out_56, out_57, out_58, out_59, out_60, out_61, out_62, out_63, out_64, out_65, out_66, out_67, out_68, out_69, out_70, out_71, out_72, out_73, out_74, out_75, out_76, out_77, out_78, out_79, out_80, out_81, out_82, out_83, out_84, out_85, out_86, out_87, out_88, out_89, out_90, out_91, out_92, out_93, out_94, out_95, out_96, out_97, out_98, out_99, out_100, out_101, out_102, out_103, out_104, out_105, out_106, out_107, out_114, out_115, out_116, out_117, out_118, out_119, out_120, out_121, out_122, out_123, out_124, out_125, out_126, out_127
  PriorityEncoder #(.Selector_Bits(4)) priorityencoder_1 (
    .in0(demultiplexer_3_out_10), .in1(demultiplexer_3_out_11), .in2(demultiplexer_3_out_12),
    .in3(demultiplexer_3_out_13), .in4(demultiplexer_3_out_14), .in5(demultiplexer_3_out_15),
    .in6(demultiplexer_3_out_16), .in7(demultiplexer_3_out_17), .in8(demultiplexer_3_out_18),
    .in9(demultiplexer_3_out_19), .in10(1'b0), .in11(1'b0), .in12(1'b0), .in13(1'b0), .in14(1'b0),
    .in15(1'b0), .num(priorityencoder_1_num), .any(priorityencoder_1_any));
  Terminal terminal_1 (.D(Data), .C(Clock), .en(demultiplexer_3_out_0));
  timer Timer_0 (
    .D(Data), .WriteUnit(demultiplexer_3_out_108), .WriteCount(demultiplexer_3_out_110),
    .Clear(demultiplexer_3_out_112), .Clock(Clock), .Q(Timer0));
  Comparator #(.Bits(8)) comparator_8 (.a(Data), .b({8{1'b0}}), .gt(comparator_8_gt[0]));  // open: eq, lt
  Register #(.Bits(8)) GFX_X (.D(Data), .C(Clock), .en(demultiplexer_3_out_30), .Q(GraphicsX));
  Register #(.Bits(8)) GFX_Y (.D(Data), .C(Clock), .en(demultiplexer_3_out_31), .Q(GraphicsY));
  Register #(.Bits(4)) register_1 (.D(Data[3:0]), .C(Clock), .en(demultiplexer_3_out_7), .Q(HEX[23:20]));
  Register #(.Bits(4)) register_2 (.D(Data[3:0]), .C(Clock), .en(demultiplexer_3_out_6), .Q(HEX[19:16]));
  BarrelShifter #(.Bits(10)) barrelshifter_4 (.in(10'h1), .shift(priorityencoder_1_num), .out(barrelshifter_4_out));
  BarrelShifter #(.Bits(10)) barrelshifter_5 (
    .in({{9{1'b0}}, comparator_8_gt[0]}), .shift(priorityencoder_1_num), .out(barrelshifter_5_out));
  Register #(.Bits(4)) register_3 (.D(Data[3:0]), .C(Clock), .en(demultiplexer_3_out_5), .Q(HEX[15:12]));
  assign or_7_out = barrelshifter_5_out | and_4_out;  // Or or_7, 10 bits wide
  timer Timer_1 (
    .D(Data), .WriteUnit(demultiplexer_3_out_109), .WriteCount(demultiplexer_3_out_111),
    .Clear(demultiplexer_3_out_113), .Clock(Clock), .Q(Timer1));
  Register #(.Bits(4)) register_4 (.D(Data[3:0]), .C(Clock), .en(demultiplexer_3_out_4), .Q(HEX[11:8]));
  assign not_3_out = ~barrelshifter_4_out;  // Not not_3, 10 bits wide
  assign and_4_out = LEDs & not_3_out;  // And and_4, 10 bits wide
  Register #(.Bits(4)) register_5 (.D(Data[3:0]), .C(Clock), .en(demultiplexer_3_out_3), .Q(HEX[7:4]));
  Register #(.Bits(10)) u_LEDs (.D(or_7_out), .C(Clock), .en(priorityencoder_1_any), .Q(LEDs));
  Register #(.Bits(4)) register_6 (.D(Data[3:0]), .C(Clock), .en(demultiplexer_3_out_2), .Q(HEX[3:0]));
  Sub #(.Bits(8)) sub_6 (.a(C0), .b(8'ha), .c_i(1'b0), .s(sub_6_s));  // open: c_o
  Sub #(.Bits(8)) sub_7 (.a(C0), .b(8'h14), .c_i(1'b0), .s(sub_7_s));  // open: c_o
  Sub #(.Bits(8)) sub_8 (.a(C0), .b(8'h2), .c_i(1'b0), .s(sub_8_s));  // open: c_o
  BarrelShifter #(.Bits(10)) barrelshifter_6 (.in(10'h1), .shift(sub_6_s[3:0]), .out(barrelshifter_6_out));
  BarrelShifter #(.Bits(10)) barrelshifter_7 (.in(10'h1), .shift(sub_7_s[3:0]), .out(barrelshifter_7_out));
  assign and_5_out = barrelshifter_6_out & LEDs;  // And and_5, 10 bits wide
  assign and_6_out = barrelshifter_7_out & Switches;  // And and_6, 10 bits wide
  Multiplexer #(.Bits(4), .Selector_Bits(3)) multiplexer_21 (
    .sel(sub_8_s[2:0]), .in_0(HEX[3:0]), .in_1(HEX[7:4]), .in_2(HEX[11:8]), .in_3(HEX[15:12]),
    .in_4(HEX[19:16]), .in_5(HEX[23:20]), .in_6(4'b0000), .in_7(4'b0000), .out(multiplexer_21_out));
  Comparator #(.Bits(10)) comparator_9 (.a(and_5_out), .b({10{1'b0}}), .gt(comparator_9_gt[0]));  // open: eq, lt
  Comparator #(.Bits(10)) comparator_10 (.a(and_6_out), .b({10{1'b0}}), .gt(comparator_10_gt[0]));  // open: eq, lt
  PRNG #(.Bits(8)) prng_1 (.S({8{1'b0}}), .se(1'b0), .ne(1'b1), .C(Clock), .R(prng_1_r));
  Multiplexer #(.Bits(8), .Selector_Bits(7)) multiplexer_22 (
    .sel(C0[6:0]), .in_0({8{1'b0}}), .in_1({8{1'b0}}), .in_2({4'b0000, multiplexer_21_out}),
    .in_3({4'b0000, multiplexer_21_out}), .in_4({4'b0000, multiplexer_21_out}),
    .in_5({4'b0000, multiplexer_21_out}), .in_6({4'b0000, multiplexer_21_out}),
    .in_7({4'b0000, multiplexer_21_out}), .in_8({{7{1'b0}}, KEY0}), .in_9({{7{1'b0}}, KEY1}),
    .in_10({{7{1'b0}}, comparator_9_gt[0]}), .in_11({{7{1'b0}}, comparator_9_gt[0]}),
    .in_12({{7{1'b0}}, comparator_9_gt[0]}), .in_13({{7{1'b0}}, comparator_9_gt[0]}),
    .in_14({{7{1'b0}}, comparator_9_gt[0]}), .in_15({{7{1'b0}}, comparator_9_gt[0]}),
    .in_16({{7{1'b0}}, comparator_9_gt[0]}), .in_17({{7{1'b0}}, comparator_9_gt[0]}),
    .in_18({{7{1'b0}}, comparator_9_gt[0]}), .in_19({{7{1'b0}}, comparator_9_gt[0]}),
    .in_20({{7{1'b0}}, comparator_10_gt[0]}), .in_21({{7{1'b0}}, comparator_10_gt[0]}),
    .in_22({{7{1'b0}}, comparator_10_gt[0]}), .in_23({{7{1'b0}}, comparator_10_gt[0]}),
    .in_24({{7{1'b0}}, comparator_10_gt[0]}), .in_25({{7{1'b0}}, comparator_10_gt[0]}),
    .in_26({{7{1'b0}}, comparator_10_gt[0]}), .in_27({{7{1'b0}}, comparator_10_gt[0]}),
    .in_28({{7{1'b0}}, comparator_10_gt[0]}), .in_29({{7{1'b0}}, comparator_10_gt[0]}), .in_30(GraphicsX),
    .in_31(GraphicsY), .in_32({8{1'b0}}), .in_33({8{1'b0}}), .in_34({8{1'b0}}), .in_35({{7{1'b0}}, WASD[0]}),
    .in_36({{7{1'b0}}, WASD[1]}), .in_37({{7{1'b0}}, WASD[2]}), .in_38({{7{1'b0}}, WASD[3]}),
    .in_39({8{1'b0}}), .in_40({8{1'b0}}), .in_41({8{1'b0}}), .in_42({8{1'b0}}), .in_43({8{1'b0}}),
    .in_44({8{1'b0}}), .in_45({8{1'b0}}), .in_46({8{1'b0}}), .in_47({8{1'b0}}), .in_48({8{1'b0}}),
    .in_49({8{1'b0}}), .in_50({8{1'b0}}), .in_51({8{1'b0}}), .in_52({8{1'b0}}), .in_53({8{1'b0}}),
    .in_54({8{1'b0}}), .in_55({8{1'b0}}), .in_56({8{1'b0}}), .in_57({8{1'b0}}), .in_58({8{1'b0}}),
    .in_59({8{1'b0}}), .in_60({8{1'b0}}), .in_61({8{1'b0}}), .in_62({8{1'b0}}), .in_63({8{1'b0}}),
    .in_64({8{1'b0}}), .in_65({8{1'b0}}), .in_66({8{1'b0}}), .in_67({8{1'b0}}), .in_68({8{1'b0}}),
    .in_69({8{1'b0}}), .in_70({8{1'b0}}), .in_71({8{1'b0}}), .in_72({8{1'b0}}), .in_73({8{1'b0}}),
    .in_74({8{1'b0}}), .in_75({8{1'b0}}), .in_76({8{1'b0}}), .in_77({8{1'b0}}), .in_78({8{1'b0}}),
    .in_79({8{1'b0}}), .in_80({8{1'b0}}), .in_81({8{1'b0}}), .in_82({8{1'b0}}), .in_83({8{1'b0}}),
    .in_84({8{1'b0}}), .in_85({8{1'b0}}), .in_86({8{1'b0}}), .in_87({8{1'b0}}), .in_88({8{1'b0}}),
    .in_89({8{1'b0}}), .in_90({8{1'b0}}), .in_91({8{1'b0}}), .in_92({8{1'b0}}), .in_93(prng_1_r),
    .in_94({8{1'b0}}), .in_95({8{1'b0}}), .in_96({8{1'b0}}), .in_97({8{1'b0}}), .in_98({8{1'b0}}),
    .in_99({8{1'b0}}), .in_100({8{1'b0}}), .in_101({8{1'b0}}), .in_102({8{1'b0}}), .in_103({8{1'b0}}),
    .in_104({8{1'b0}}), .in_105({8{1'b0}}), .in_106({8{1'b0}}), .in_107({8{1'b0}}), .in_108({8{1'b0}}),
    .in_109({8{1'b0}}), .in_110({8{1'b0}}), .in_111({8{1'b0}}), .in_112({{7{1'b0}}, Timer0}),
    .in_113({{7{1'b0}}, Timer1}), .in_114({8{1'b0}}), .in_115({8{1'b0}}), .in_116({8{1'b0}}),
    .in_117({8{1'b0}}), .in_118({8{1'b0}}), .in_119({8{1'b0}}), .in_120({8{1'b0}}), .in_121({8{1'b0}}),
    .in_122({8{1'b0}}), .in_123({8{1'b0}}), .in_124({8{1'b0}}), .in_125({8{1'b0}}), .in_126({8{1'b0}}),
    .in_127({8{1'b0}}), .out(PortIn));

  // Other names for the same wires on the sheet: Mode1 = Mode[0]; Mode2[1:0] = Mode[1:0]

  // Notes on the sheet:
  //   Clock: Hz: 2147483647
  //   Control Logic
  //   Data Flow
  //   Memory Bus
  //   User Interface
  //   contents of Program (hex, n*v repeats v):
  //   74,0,40,90,4,1,20,61,20,6b,4,0,20,0,94,9c,92,6,0,98,0,18,96,9c
  //   ,90,92,93,c,80,5,20,0,2c,7c,f8,97,96,94,9c,90,20,1,1c,1,84,fa
  //   ,94,9c,50,72,65,73,73,65,64,20,42,75,74,74,6f,6e,20,0,98,0,3,4
  //   ,7,34,16,89,44,16,34,c,8d,44,c,28,85,f3,1c,14,1d,8,59,20,a,1c
  //   ,15,1d,9,61,20,b,4,9,24,18,80,1,2c,30,28,89,80,1e,d,84,1b,93,7
  //   ,30,98,0,10,97,10,80,2,9,80,2,4,30,44,8,39,20,0,8,80,2,5,a,21
  //   ,0,89,15,6c,8,84,d7,4,2,10,80,2,88,24,10,80,3,6c,a,8,80,2,9,80
  //   ,3,81,9,5,0,8d,24,6c,8,81,e6,28,8d,7c,93
  //   ALU
  //   contents of Microcode (hex, n*v repeats v):
  //   800000,9*0,a60164,7*0,220464,0,220564,3,860167,0,0,2,860166,7*0
  //   ,220464,0,220564,820617,0,0,0,820616,8*0,220264,0,a20364,5*0,220464
  //   ,860194,6*0,220464,820714,4*0,860118,7*0,86011c,7*0,60338,81034
  //   ,860228,5*0,6033c,81834,86022c,7*0,220464,860040,4*0,860010,9*0
  //   ,220464,860840,4*0,860810,9*0,220464,861040,4*0,861010,9*0,220464
  //   ,861840,4*0,861810,9*0,220464,862040,4*0,862010,9*0,220464,862840
  //   ,4*0,862810,9*0,220464,863040,4*0,863010,9*0,220464,843840,4*0
  //   ,843810,9*0,220464,0,220564,c00800,0,0,c00000,9*0,401064,a00000
  //   ,6*0,220464,80800,c01044,5*0,220464,80000,c01044,4*0,20404,860194
  //   ,6*0,20404,820714,5*0,8000,820615,7*0,1,838165,7*0,220464,0,228564
  //   ,28675,20685,c00800,0,1,38465,1,38565,c00800,0,0,0,100000,6*0
  //   ,864010,7*0,864810,7*0,865010
  //   Special Registers
  //   Port Write
  //   Port Read
  //   contents of Microcode (hex, n*v repeats v):
  //   800000,9*0,a60164,7*0,220464,0,220564,3,860167,0,0,2,860166,7*0 ,220464,0,220564,820617,0,0,
  //   0,820616,8*0,220264,0,a20364,5*0,220464 ,860194,6*0,220464,820714,4*0,860118,7*0,86011c,7*0,
  //   60338,81034 ,860228,5*0,6033c,81834,86022c,7*0,220464,860040,4*0,860010,9*0 ,220464,860840,
  //   4*0,860810,9*0,220464,861040,4*0,861010,9*0,220464 ,861840,4*0,861810,9*0,220464,862040,4*0,
  //   862010,9*0,220464,862840 ,4*0,862810,9*0,220464,863040,4*0,863010,9*0,220464,843840,4*0 ,843810,
  //   9*0,220464,0,220564,c00800,0,0,c00000,9*0,401064,a00000 ,6*0,220464,80800,c01044,5*0,220464,
  //   80000,c01044,4*0,20404,860194 ,6*0,20404,820714,5*0,8000,820615,7*0,1,838165,7*0,220464,0,228564 ,
  //   28675,20685,c00800,0,1,38465,1,38565,c00800,0,0,0,100000,6*0 ,864010,7*0,864810,7*0,865010
endmodule
