// Logisim project simulation.circ as structural Verilog
module main (
);

  wire addr_override_en, and_1_out, and_2_out, and_5_out, and_18_out, btn0, btn1, clear_screen, clk,
       clk_btn_out, clock_2_out, comparator_1_gt, comparator_2_lt, comparator_3_eq, comparator_3_lt,
       comparator_4_lt, comparator_5_eq, comparator_6_eq, comparator_7_eq, comparator_7_lt, comparator_8_eq,
       comparator_8_lt, comparator_9_gt, comparator_10_gt, comparator_11_gt, comparator_12_gt,
       comparator_13_gt, comparator_15_eq, comparator_16_gt, comparator_17_gt, comparator_18_gt,
       comparator_19_gt, comparator_20_gt, cond_en, DE10_clk, decoder_1_out0, decoder_1_out1, decoder_1_out2,
       decoder_1_out3, decoder_2_out2, decoder_2_out3, decoder_2_out4, decoder_2_out5, decoder_2_out6,
       decoder_2_out7, decoder_2_out10, decoder_2_out11, decoder_2_out12, decoder_2_out13, decoder_2_out14,
       decoder_2_out15, decoder_2_out16, decoder_2_out17, decoder_2_out18, decoder_2_out19, decoder_2_out30,
       decoder_2_out31, decoder_3_out3, decoder_3_out4, decoder_3_out5, decoder_3_out6, decoder_3_out7,
       decoder_3_out8, decoder_3_out9, decoder_3_out10, decoder_3_out11, decoder_3_out12, decoder_3_out13,
       decoder_3_out14, decoder_3_out15, decoder_3_out16, decoder_3_out17, decoder_3_out18, decoder_3_out19,
       decoder_3_out20, decoder_3_out21, decoder_3_out22, decoder_3_out23, decoder_3_out24, decoder_3_out25,
       decoder_3_out26, decoder_3_out27, decoder_3_out28, decoder_3_out29, decoder_3_out30, decoder_3_out31,
       decoder_4_out0, decoder_4_out1, decoder_4_out2, decoder_4_out3, decoder_4_out4, decoder_4_out5,
       decoder_4_out6, decoder_4_out7, decoder_4_out8, decoder_4_out9, decoder_4_out10, decoder_4_out11,
       decoder_4_out12, decoder_4_out13, decoder_4_out14, decoder_4_out15, decoder_4_out16, decoder_4_out17,
       decoder_4_out18, decoder_4_out19, decoder_4_out20, decoder_4_out21, decoder_4_out22, decoder_4_out31,
       decoder_5_out0, decoder_5_out1, decoder_5_out2, decoder_5_out3, decoder_5_out4, decoder_5_out5,
       decoder_5_out6, decoder_5_out7, decoder_5_out8, decoder_5_out9, decoder_5_out10, decoder_5_out11,
       decoder_5_out12, decoder_5_out13, decoder_5_out14, decoder_5_out15, decoder_5_out16, decoder_5_out17,
       decoder_6_out0, decoder_6_out1, decoder_6_out2, decoder_6_out3, decoder_6_out4, decoder_6_out5,
       decoder_7_out0, decoder_7_out1, decoder_7_out2, decoder_7_out3, draw_pixel, draw_sprite, F_write,
       gfx_clear_freeze, gfx_swap, halt, halted, mem_write, multiplexer_2_out, multiplexer_4_out, not_1_out,
       not_2_out, or_1_out, or_2_out, or_3_out, or_5_out, or_6_out, or_7_out, or_8_out, or_10_out, or_11_out,
       or_12_out, or_18_out, port_write, priority_encoder_1_gs, priority_encoder_2_gs, SP_en, SP_inc,
       timer_out_0, timer_out_1, tx, uart_en, uart_freeze, uart_out, uart_pop, VGA_port_p15, write, ws2812,
       ws2812_en;
  wire [1:0] addr_mode, cond, VGA_port_p8, write_op_sel;
  wire [1:1] clocks_port_p3;
  wire [2:0] timer_mode_0, timer_mode_1, write_sel;
  wire [2:2] subtractor_4_bout;
  wire [3:0] adder_6_out, alu_1_flags_out, and_17_out, bit_extender_14_out, bit_extender_17_out, F, F_val,
       instr_state, Instr_State_q, mode, multiplexer_5_out, multiplexer_6_out, multiplexer_23_out,
       multiplexer_26_out, or_20_out, priority_encoder_1_out, priority_encoder_2_out, read_sel,
       subtractor_1_out, VGA_port_p10, VGA_port_p11, VGA_port_p12;
  wire [3:2] adder_11_cout;
  wire [4:0] subtractor_5_out, subtractor_6_out, subtractor_7_out, subtractor_9_out;
  wire [5:0] bit_extender_10_out, bit_extender_12_out;
  wire [6:0] adder_4_out, multiplexer_7_out, rgb_video_1_p4, sprite_q;
  wire [7:0] A, adc_0, adc_1, adc_2, adc_3, adc_4, adc_5, adder_8_out, adder_9_out, adder_10_out,
       adder_11_out, alu_1_result, B, bit_extender_5_out, bit_extender_6_out, bit_extender_7_out,
       bit_extender_24_out, bit_extender_25_out, bit_extender_26_out, bit_extender_27_out,
       bit_extender_28_out, bit_extender_29_out, bit_extender_30_out, bit_extender_31_out,
       bit_extender_32_out, bit_extender_33_out, bit_extender_34_out, bit_extender_35_out, C0, C1, data,
       gfx_x, gfx_y, H, Instr_q, L, mem, mem_val, multiplexer_9_out, multiplexer_12_out, multiplexer_13_out,
       multiplexer_14_out, multiplexer_15_out, multiplexer_16_out, multiplexer_17_out, multiplexer_19_out,
       multiplexer_20_out, multiplexer_28_out, multiplexer_29_out, multiplexer_30_out, multiplexer_31_out,
       negator_1_out, port_in, Program_data, PWM_3_q, PWM_5_q, PWM_6_q, PWM_9_q, PWM_10_q, PWM_11_q,
       RAM_1_dout, random_1_out, shifter_1_out, SP, subtractor_2_out, subtractor_3_out, subtractor_4_out,
       subtractor_8_out, timer_count_0, timer_count_1, uart_available, uart_in;
  wire [7:2] instr;
  wire [8:0] bit_extender_3_out, bit_extender_4_out, multiplier_1_out;
  wire [9:0] and_6_out, and_19_out, and_20_out, bit_extender_9_out, leds, not_3_out, or_9_out, shifter_2_out,
       shifter_3_out, shifter_18_out, shifter_19_out, switches;
  wire [11:3] PWM_driver_0_modulated;
  wire [14:0] adder_5_out, multiplexer_8_out, pixel_q;
  wire [15:0] adder_1_out, adder_2_out, adder_3_out, addr_override, and_8_out, and_10_out, and_11_out,
       and_12_out, and_13_out, and_14_out, and_15_out, and_16_out, and_22_out, Arduino_in, Arduino_mode_q,
       Arduino_out_q, Arduino_port_p2, bit_extender_1_out, bit_extender_2_out, bit_extender_15_out,
       bit_extender_16_out, bit_extender_18_out, bit_extender_19_out, bit_extender_20_out,
       bit_extender_21_out, bit_extender_22_out, bit_extender_23_out, multiplexer_1_out, multiplexer_3_out,
       multiplexer_24_out, multiplexer_25_out, not_5_out, not_7_out, not_8_out, not_9_out, not_10_out,
       not_11_out, or_15_out, or_16_out, or_19_out, PC, pwm_en_q, shifter_8_out, shifter_9_out,
       shifter_10_out, shifter_11_out, shifter_12_out, shifter_13_out, shifter_14_out, shifter_15_out,
       shifter_16_out, shifter_17_out, shifter_21_out;
  wire [23:0] Microcode_data, seven_seg;
  wire [35:0] and_7_out, and_9_out, and_21_out, bit_extender_11_out, bit_extender_13_out, GPIO_in,
       GPIO_mode_q, GPIO_out_q, not_4_out, not_6_out, or_13_out, or_14_out, shifter_4_out, shifter_5_out,
       shifter_6_out, shifter_7_out, shifter_20_out;

  Register #(.width(16)) u_PC (.D(multiplexer_1_out), .en(or_1_out), .clk(clk), .Q(PC));  // open: clr
  Multiplexer #(.enable("false"), .width(16)) multiplexer_1 (
    .in0(adder_2_out), .in1(multiplexer_3_out), .out(multiplexer_1_out), .sel(Microcode_data[22]));
  or or_1 (or_1_out, comparator_6_eq, Microcode_data[22], Microcode_data[21]);
  Multiplexer #(.enable("false"), .select(2)) multiplexer_2 (
    .in0(F[3]), .in1(F[2]), .in2(F[1]), .in3(F[0]), .out(multiplexer_2_out), .sel(cond));
  Comparator #(.mode("unsigned")) comparator_1 (.a(data), .b({8{1'b0}}), .gt(comparator_1_gt));  // open: eq, lt
  Comparator #(.mode("unsigned")) comparator_2 (.a(data), .b({8{1'b1}}), .lt(comparator_2_lt));  // open: gt, eq
  LED halted_led (.in(halted));
  LED clk_led (.in(clk));
  Hex_Digit_Display PC_0 (.value(PC[3:0]));  // open: dp
  Multiplexer #(.enable("false"), .select(2), .width(16)) multiplexer_3 (
    .in0({H, L}), .in1({C0, C1}), .in2(adder_1_out), .out(multiplexer_3_out), .sel(mode[1:0]));  // open: in3
  not not_1 (not_1_out, multiplexer_2_out);
  Multiplexer #(.enable("false"), .select(2)) multiplexer_4 (
    .in0(multiplexer_2_out), .in1(not_1_out), .in2(comparator_1_gt), .in3(comparator_2_lt),
    .out(multiplexer_4_out), .sel(mode[1:0]));
  Hex_Digit_Display PC_1 (.value(PC[7:4]));  // open: dp
  Hex_Digit_Display PC_2 (.value(PC[11:8]));  // open: dp
  // PortIO clocks_port: pin names not known; wires that end beside it: 1'b0, 2'b00, {clocks_port_p3[1], DE10_clk}
  assign bit_extender_1_out = {{8{data[7]}}, data};  // Bit_Extender bit_extender_1
  Adder #(.width(16)) adder_1 (.a(bit_extender_1_out), .b(PC), .out(adder_1_out));  // open: cin, cout
  Adder #(.width(16)) adder_2 (.a(PC), .b(16'h1), .out(adder_2_out));  // open: cin, cout
  or or_2 (or_2_out, uart_freeze, addr_override_en, gfx_clear_freeze, halted);
  and and_1 (and_1_out, cond_en, multiplexer_4_out);
  Comparator #(.mode("unsigned"), .width(4)) comparator_3 (
    .a(instr_state), .b(4'b0001), .eq(comparator_3_eq), .lt(comparator_3_lt));  // open: gt
  Button clk_btn (.out(clk_btn_out));
  Clock clock_1 (.out(clk));
  TTY tty_1 (.data(data[6:0]), .clk(clk), .we(uart_out));  // open: clr
  Hex_Digit_Display PC_3 (.value(PC[15:12]));  // open: dp
  Register u_Instr (.D(mem), .en(comparator_6_eq), .clk(clk), .Q(Instr_q));  // open: clr
  Register #(.width(4)) u_Instr_State (.D(multiplexer_5_out), .en(1'b1), .clk(clk), .Q(Instr_State_q));  // open: clr
  Multiplexer #(.enable("false"), .width(4)) multiplexer_5 (
    .in0(multiplexer_6_out), .in1(Instr_State_q), .out(multiplexer_5_out), .sel(or_2_out));
  Multiplexer #(.enable("false"), .width(4)) multiplexer_6 (
    .in0(adder_6_out), .in1(4'b0000), .out(multiplexer_6_out), .sel(or_3_out));
  Register #(.width(1)) u_Halted (.D(1'b1), .en(and_2_out), .clk(clk), .Q(halted), .clr(comparator_3_lt));
  and and_2 (and_2_out, halt, comparator_3_eq);
  Hex_Digit_Display A_0 (.value(A[3:0]));  // open: dp
  Hex_Digit_Display A_1 (.value(A[7:4]));  // open: dp
  Hex_Digit_Display H_0 (.value(H[3:0]));  // open: dp
  Hex_Digit_Display H_1 (.value(H[7:4]));  // open: dp
  Register #(.width(7)) sprite (.D(multiplexer_7_out), .en(draw_sprite), .clk(clk), .Q(sprite_q));  // open: clr
  Multiplexer #(.enable("false"), .width(7)) multiplexer_7 (
    .in0(adder_4_out), .in1({7{1'b0}}), .out(multiplexer_7_out), .sel(comparator_7_eq));
  Register #(.width(15)) pixel (.D(multiplexer_8_out), .en(clear_screen), .clk(clk), .Q(pixel_q));  // open: clr
  Multiplexer #(.enable("false"), .width(15)) multiplexer_8 (
    .in0(adder_5_out), .in1({15{1'b0}}), .out(multiplexer_8_out), .sel(comparator_8_eq));
  not not_2 (not_2_out, comparator_4_lt);
  or or_3 (or_3_out, and_1_out, Microcode_data[23]);
  Hex_Digit_Display B_0 (.value(B[3:0]));  // open: dp
  Hex_Digit_Display L_0 (.value(L[3:0]));  // open: dp
  Adder #(.width(16)) adder_3 (.a({H, L}), .b(bit_extender_2_out), .out(adder_3_out));  // open: cin, cout
  assign bit_extender_2_out = {{9{1'b0}}, sprite_q};  // Bit_Extender bit_extender_2
  Adder #(.width(7)) adder_4 (.a(sprite_q), .b(7'b0000001), .out(adder_4_out));  // open: cin, cout
  Adder #(.width(15)) adder_5 (.a(pixel_q), .b(15'h1), .out(adder_5_out));  // open: cin, cout
  Multiplexer #(.enable("false"), .width(8)) multiplexer_9 (
    .in0(mem), .in1(Instr_q), .out(multiplexer_9_out), .sel(not_2_out));
  Multiplexer #(.enable("false"), .width(8)) multiplexer_10 (
    .in0(multiplexer_9_out), .in1(8'h4), .out({instr, cond}), .sel(comparator_5_eq));
  Comparator #(.mode("unsigned"), .width(4)) comparator_4 (
    .a(Instr_State_q), .b(4'b0010), .lt(comparator_4_lt));  // open: gt, eq
  Comparator #(.mode("unsigned"), .width(4)) comparator_5 (
    .a(Instr_State_q), .b(4'b0000), .eq(comparator_5_eq));  // open: gt, lt
  Comparator #(.mode("unsigned"), .width(4)) comparator_6 (
    .a(Instr_State_q), .b(4'b0001), .eq(comparator_6_eq));  // open: gt, lt
  Adder #(.width(4)) adder_6 (.a(Instr_State_q), .b(4'b0001), .out(adder_6_out));  // open: cin, cout
  Hex_Digit_Display B_1 (.value(B[7:4]));  // open: dp
  Hex_Digit_Display L_1 (.value(L[7:4]));  // open: dp
  Adder #(.width(16)) adder_7 (.a({16{1'b0}}), .b(adder_3_out), .out(addr_override));  // open: cin, cout
  Comparator #(.mode("unsigned"), .width(7)) comparator_7 (
    .a(sprite_q), .b(7'b1000000), .eq(comparator_7_eq), .lt(comparator_7_lt));  // open: gt
  Comparator #(.mode("unsigned")) comparator_8 (
    .a(pixel_q[14:7]), .b(8'ha0), .eq(comparator_8_eq), .lt(comparator_8_lt));  // open: gt
  // Probe on {instr, cond}
  Shifter #(.shift("lr")) shifter_1 (.in({instr, cond}), .\dist (3'b010), .out(shifter_1_out));
  Multiplexer #(.enable("false"), .width(4)) multiplexer_11 (
    .in0(subtractor_1_out), .in1(4'b0000), .out(instr_state), .sel(comparator_5_eq));
  Subtractor #(.width(4)) subtractor_1 (.a(Instr_State_q), .b(4'b0001), .out(subtractor_1_out));  // open: bin, bout
  LED LED_9 (.in(leds[9]));
  Hex_Digit_Display instr_0 (.value({instr[3:2], cond}));  // open: dp
  and and_3 (addr_override_en, comparator_7_lt, draw_sprite);
  Comparator #(.mode("unsigned")) comparator_9 (.a(mem), .b({8{1'b0}}), .gt(comparator_9_gt));  // open: eq, lt
  and and_4 (gfx_clear_freeze, comparator_8_lt, clear_screen);
  assign bit_extender_3_out = {{1{1'b0}}, shifter_1_out};  // Bit_Extender bit_extender_3
  assign bit_extender_4_out = {{5{1'b0}}, instr_state};  // Bit_Extender bit_extender_4
  Register #(.width(4)) u_F (.D(F_val), .en(F_write), .clk(clk), .Q(F));  // open: clr
  LED LED_8 (.in(leds[8]));
  LED LED_7 (.in(leds[7]));
  LED LED_6 (.in(leds[6]));
  LED LED_5 (.in(leds[5]));
  Button Button_1 (.out(btn0));
  Button Button_2 (.out(btn1));
  Hex_Digit_Display instr_1 (.value(instr[7:4]));  // open: dp
  and and_5 (and_5_out, comparator_9_gt, comparator_7_lt, draw_sprite);
  ROM #(.addrWidth(9), .dataWidth(24)) Microcode (
    .addr(multiplier_1_out),
    .data({Microcode_data[23:21], halt, cond_en, F_write, write, SP_inc, SP_en, mode, write_sel, read_sel, write_op_sel, Microcode_data[1:0]}));
  Multiplier #(.width(9)) multiplier_1 (
    .a(bit_extender_3_out), .b(9'h8), .out(multiplier_1_out), .cin(bit_extender_4_out));  // open: cout
  // Probe on F
  LED LED_4 (.in(leds[4]));
  LED LED_3 (.in(leds[3]));
  LED LED_2 (.in(leds[2]));
  LED LED_1 (.in(leds[1]));
  buf or_4 (uart_freeze, 1'b0);  // OR_Gate
  assign bit_extender_5_out = {{5{1'b0}}, sprite_q[2:0]};  // Bit_Extender bit_extender_5
  assign bit_extender_6_out = {{5{1'b0}}, sprite_q[5:3]};  // Bit_Extender bit_extender_6
  or or_5 (or_5_out, and_5_out, gfx_clear_freeze, draw_pixel);
  LED LED_0 (.in(leds[0]));
  Hex_Digit_Display instruction_state (.value(instr_state));  // open: dp
  Adder adder_8 (.a(gfx_x), .b(bit_extender_5_out), .out(adder_8_out));  // open: cin, cout
  Adder adder_9 (.a(gfx_y), .b(bit_extender_6_out), .out(adder_9_out));  // open: cin, cout
  Register u_SP (.D(multiplexer_17_out), .en(SP_en), .clk(clk), .Q(SP));  // open: clr
  // DipSwitch #(.number(10)) DipSwitch_1: pin names not known; wires that end beside it: switches[0], switches[1], switches[2], switches[3], switches[4], switches[5], switches[6], switches[7], switches[8], switches[9]
  Hex_Digit_Display C0_0 (.value(C0[3:0]));  // open: dp
  Multiplexer #(.enable("false"), .width(8)) multiplexer_12 (
    .in0(data), .in1(mem), .out(multiplexer_12_out), .sel(draw_sprite));
  Multiplexer #(.enable("false"), .width(8)) multiplexer_13 (
    .in0(gfx_x), .in1(adder_8_out), .out(multiplexer_13_out), .sel(draw_sprite));
  Multiplexer #(.enable("false"), .width(8)) multiplexer_14 (
    .in0(gfx_y), .in1(adder_9_out), .out(multiplexer_14_out), .sel(draw_sprite));
  assign bit_extender_7_out = {{1{1'b0}}, pixel_q[6:0]};  // Bit_Extender bit_extender_7
  Hex_Digit_Display HEX5 (.value(seven_seg[23:20]));  // open: dp
  Hex_Digit_Display C0_1 (.value(C0[7:4]));  // open: dp
  Multiplexer #(.enable("false"), .width(8)) multiplexer_15 (
    .in0(multiplexer_13_out), .in1(pixel_q[14:7]), .out(multiplexer_15_out), .sel(clear_screen));
  Multiplexer #(.enable("false"), .width(8)) multiplexer_16 (
    .in0(multiplexer_14_out), .in1(bit_extender_7_out), .out(multiplexer_16_out), .sel(clear_screen));
  // Probe on cond
  Adder adder_10 (.a(SP), .b(8'h1), .out(adder_10_out));  // open: cin, cout
  Multiplexer #(.enable("false"), .width(8)) multiplexer_17 (
    .in0(adder_10_out), .in1(subtractor_2_out), .out(multiplexer_17_out), .sel(SP_inc));
  Subtractor subtractor_2 (.a(SP), .b(8'h1), .out(subtractor_2_out));  // open: bin, bout
  Hex_Digit_Display HEX4 (.value(seven_seg[19:16]));  // open: dp
  Hex_Digit_Display HEX3 (.value(seven_seg[15:12]));  // open: dp
  Hex_Digit_Display C1_0 (.value(C1[3:0]));  // open: dp
  Multiplexer #(.enable("false"), .width(2)) multiplexer_18 (
    .in0(Microcode_data[1:0]), .in1(2'b00), .out(addr_mode), .sel(comparator_5_eq));
  // Probe on write_op_sel
  // Probe on read_sel
  // Probe on write_sel
  // Probe on mode
  Hex_Digit_Display HEX2 (.value(seven_seg[11:8]));  // open: dp
  Hex_Digit_Display HEX1 (.value(seven_seg[7:4]));  // open: dp
  Hex_Digit_Display C1_1 (.value(C1[7:4]));  // open: dp
  // RGB_Video #(.width(256)) rgb_video_1: pin names not known; wires that end beside it: clk, or_5_out, multiplexer_15_out, rgb_video_1_p4, multiplexer_12_out
  Bit_Extender #(.out_width(7), .\type ("zero")) bit_extender_8 (.in(multiplexer_16_out), .out(rgb_video_1_p4));
  // Probe on Microcode_data[1:0]
  Hex_Digit_Display HEX0 (.value(seven_seg[3:0]));  // open: dp
  Hex_Digit_Display gfx_x0 (.value(gfx_x[3:0]));  // open: dp
  Hex_Digit_Display gfx_x1 (.value(gfx_x[7:4]));  // open: dp
  Hex_Digit_Display gfx_y0 (.value(gfx_y[3:0]));  // open: dp
  Hex_Digit_Display adc0 (.value(adc_0[3:0]));  // open: dp
  // PortIO VGA_port: pin names not known; wires that end beside it: DE10_clk, gfx_swap, multiplexer_12_out, multiplexer_15_out, multiplexer_16_out, clk, or_5_out, VGA_port_p8[0], VGA_port_p8[1], VGA_port_p10, VGA_port_p11, VGA_port_p12, 1'b1, {VGA_port_p12, VGA_port_p11, VGA_port_p10, VGA_port_p8}, VGA_port_p15, VGA_port_p15
  Hex_Digit_Display gfx_y1 (.value(gfx_y[7:4]));  // open: dp
  Hex_Digit_Display adc1 (.value(adc_0[7:4]));  // open: dp
  // Probe on C0
  Decoder #(.select(2)) decoder_1 (
    .out0(decoder_1_out0), .out1(decoder_1_out1), .out2(decoder_1_out2), .out3(decoder_1_out3),
    .sel(C0[6:5]), .en(port_write));
  Decoder #(.select(5)) decoder_2 (
    .out0(uart_out), .out1(uart_pop), .out2(decoder_2_out2), .out3(decoder_2_out3), .out4(decoder_2_out4),
    .out5(decoder_2_out5), .out6(decoder_2_out6), .out7(decoder_2_out7), .out10(decoder_2_out10),
    .out11(decoder_2_out11), .out12(decoder_2_out12), .out13(decoder_2_out13), .out14(decoder_2_out14),
    .out15(decoder_2_out15), .out16(decoder_2_out16), .out17(decoder_2_out17), .out18(decoder_2_out18),
    .out19(decoder_2_out19), .out30(decoder_2_out30), .out31(decoder_2_out31), .sel(C0[4:0]),
    .en(decoder_1_out0));  // open: out8, out9, out20, out21, out22, out23, out24, out25, out26, out27, out28, out29
  Decoder #(.select(5)) decoder_3 (
    .out0(draw_pixel), .out1(draw_sprite), .out2(clear_screen), .out3(decoder_3_out3), .out4(decoder_3_out4),
    .out5(decoder_3_out5), .out6(decoder_3_out6), .out7(decoder_3_out7), .out8(decoder_3_out8),
    .out9(decoder_3_out9), .out10(decoder_3_out10), .out11(decoder_3_out11), .out12(decoder_3_out12),
    .out13(decoder_3_out13), .out14(decoder_3_out14), .out15(decoder_3_out15), .out16(decoder_3_out16),
    .out17(decoder_3_out17), .out18(decoder_3_out18), .out19(decoder_3_out19), .out20(decoder_3_out20),
    .out21(decoder_3_out21), .out22(decoder_3_out22), .out23(decoder_3_out23), .out24(decoder_3_out24),
    .out25(decoder_3_out25), .out26(decoder_3_out26), .out27(decoder_3_out27), .out28(decoder_3_out28),
    .out29(decoder_3_out29), .out30(decoder_3_out30), .out31(decoder_3_out31), .sel(C0[4:0]),
    .en(decoder_1_out1));
  Decoder #(.select(5)) decoder_4 (
    .out0(decoder_4_out0), .out1(decoder_4_out1), .out2(decoder_4_out2), .out3(decoder_4_out3),
    .out4(decoder_4_out4), .out5(decoder_4_out5), .out6(decoder_4_out6), .out7(decoder_4_out7),
    .out8(decoder_4_out8), .out9(decoder_4_out9), .out10(decoder_4_out10), .out11(decoder_4_out11),
    .out12(decoder_4_out12), .out13(decoder_4_out13), .out14(decoder_4_out14), .out15(decoder_4_out15),
    .out16(decoder_4_out16), .out17(decoder_4_out17), .out18(decoder_4_out18), .out19(decoder_4_out19),
    .out20(decoder_4_out20), .out21(decoder_4_out21), .out22(decoder_4_out22), .out30(gfx_swap),
    .out31(decoder_4_out31), .sel(C0[4:0]), .en(decoder_1_out2));  // open: out23, out24, out25, out26, out27, out28, out29
  Decoder #(.select(5)) decoder_5 (
    .out0(decoder_5_out0), .out1(decoder_5_out1), .out2(decoder_5_out2), .out3(decoder_5_out3),
    .out4(decoder_5_out4), .out5(decoder_5_out5), .out6(decoder_5_out6), .out7(decoder_5_out7),
    .out8(decoder_5_out8), .out9(decoder_5_out9), .out10(decoder_5_out10), .out11(decoder_5_out11),
    .out12(decoder_5_out12), .out13(decoder_5_out13), .out14(decoder_5_out14), .out15(decoder_5_out15),
    .out16(decoder_5_out16), .out17(decoder_5_out17), .sel(C0[4:0]), .en(decoder_1_out3));  // open: out18, out19, out20, out21, out22, out23, out24, out25, out26, out27, out28, out29, out30, out31
  Priority_Encoder #(.select(4)) priority_encoder_1 (
    .in0(decoder_2_out10), .in1(decoder_2_out11), .in2(decoder_2_out12), .in3(decoder_2_out13),
    .in4(decoder_2_out14), .in5(decoder_2_out15), .in6(decoder_2_out16), .in7(decoder_2_out17),
    .in8(decoder_2_out18), .in9(decoder_2_out19), .out(priority_encoder_1_out), .gs(priority_encoder_1_gs),
    .en_in(1'b1));  // open: in10, in11, in12, in13, in14, in15, en_out
  or or_6 (or_6_out, decoder_3_out3, decoder_3_out4, decoder_3_out5, decoder_3_out6, decoder_3_out7, decoder_3_out8, decoder_3_out9, decoder_3_out10, decoder_3_out11, decoder_3_out12, decoder_3_out13, decoder_3_out14, decoder_3_out15, decoder_3_out16, decoder_3_out17, decoder_3_out18, decoder_3_out19, decoder_3_out20, decoder_3_out21, decoder_3_out22, decoder_3_out23, decoder_3_out24, decoder_3_out25, decoder_3_out26, decoder_3_out27, decoder_3_out28, decoder_3_out29, decoder_3_out30, decoder_3_out31, decoder_4_out0, decoder_4_out1, decoder_4_out2, decoder_4_out3, decoder_4_out4, decoder_4_out5, decoder_4_out6);
  Priority_Encoder #(.select(4)) priority_encoder_2 (
    .in0(decoder_4_out7), .in1(decoder_4_out8), .in2(decoder_4_out9), .in3(decoder_4_out10),
    .in4(decoder_4_out11), .in5(decoder_4_out12), .in6(decoder_4_out13), .in7(decoder_4_out14),
    .in8(decoder_4_out15), .in9(decoder_4_out16), .in10(decoder_4_out17), .in11(decoder_4_out18),
    .in12(decoder_4_out19), .in13(decoder_4_out20), .in14(decoder_4_out21), .in15(decoder_4_out22),
    .out(priority_encoder_2_out), .gs(priority_encoder_2_gs));  // open: en_out, en_in
  or or_7 (or_7_out, decoder_4_out31, decoder_5_out0);
  Register #(.width(4)) register_1 (.D(data[3:0]), .en(decoder_2_out2), .clk(clk), .Q(seven_seg[3:0]));  // open: clr
  assign bit_extender_9_out = {{9{1'b0}}, comparator_10_gt};  // Bit_Extender bit_extender_9
  Comparator #(.mode("unsigned")) comparator_10 (.a(data), .b({8{1'b0}}), .gt(comparator_10_gt));  // open: eq, lt
  or or_8 (or_8_out, decoder_5_out1, decoder_5_out2);
  Decoder #(.select(3)) decoder_6 (
    .out0(decoder_6_out0), .out1(decoder_6_out1), .out2(decoder_6_out2), .out3(decoder_6_out3),
    .out4(decoder_6_out4), .out5(decoder_6_out5), .out6(mem_write), .out7(port_write), .sel(write_sel),
    .en(write));
  Register #(.width(4)) register_2 (.D(data[3:0]), .en(decoder_2_out3), .clk(clk), .Q(seven_seg[7:4]));  // open: clr
  Shifter #(.width(10)) shifter_2 (.in(10'h1), .\dist (priority_encoder_1_out), .out(shifter_2_out));
  Shifter #(.width(10)) shifter_3 (.in(bit_extender_9_out), .\dist (priority_encoder_1_out), .out(shifter_3_out));
  assign and_6_out = not_3_out & leds;  // AND_Gate and_6, 10 bits wide
  Bit_Extender #(.out_width(6), .\type ("zero")) bit_extender_10 (.in(subtractor_3_out), .out(bit_extender_10_out));
  Subtractor subtractor_3 (.a(C0), .b(8'h23), .out(subtractor_3_out));  // open: bin, bout
  assign bit_extender_11_out = {{35{1'b0}}, comparator_11_gt};  // Bit_Extender bit_extender_11
  Comparator #(.mode("unsigned")) comparator_11 (.a(data), .b({8{1'b0}}), .gt(comparator_11_gt));  // open: eq, lt
  Bit_Extender #(.out_width(6), .\type ("zero")) bit_extender_12 (.in(data), .out(bit_extender_12_out));
  assign bit_extender_13_out = {{35{1'b0}}, decoder_4_out31};  // Bit_Extender bit_extender_13
  Comparator #(.mode("unsigned")) comparator_12 (.a(data), .b({8{1'b0}}), .gt(comparator_12_gt));  // open: eq, lt
  Bit_Extender #(.out_width(4), .\type ("zero")) bit_extender_14 (.in(data), .out(bit_extender_14_out));
  assign bit_extender_15_out = {{15{1'b0}}, decoder_5_out1};  // Bit_Extender bit_extender_15
  Decoder #(.select(2)) decoder_7 (
    .out0(decoder_7_out0), .out1(decoder_7_out1), .out2(decoder_7_out2), .out3(decoder_7_out3), .sel(cond),
    .en(decoder_6_out1));
  Register #(.width(4)) register_3 (.D(data[3:0]), .en(decoder_2_out4), .clk(clk), .Q(seven_seg[11:8]));  // open: clr
  assign not_3_out = ~shifter_2_out;  // NOT_Gate not_3, 10 bits wide
  Register #(.width(10)) u_LEDs (.D(or_9_out), .en(priority_encoder_1_gs), .clk(clk), .Q(leds));  // open: clr
  assign or_9_out = shifter_3_out | and_6_out;  // OR_Gate or_9, 10 bits wide
  Shifter #(.width(36)) shifter_4 (.in(36'h1), .\dist (bit_extender_10_out), .out(shifter_4_out));
  Shifter #(.width(36)) shifter_5 (.in(bit_extender_11_out), .\dist (bit_extender_10_out), .out(shifter_5_out));
  Shifter #(.width(36)) shifter_6 (.in(36'h1), .\dist (bit_extender_12_out), .out(shifter_6_out));
  Shifter #(.width(36)) shifter_7 (.in(bit_extender_13_out), .\dist (bit_extender_12_out), .out(shifter_7_out));
  assign and_7_out = not_4_out & GPIO_mode_q;  // AND_Gate and_7, 36 bits wide
  Shifter #(.width(16)) shifter_8 (.in(16'h1), .\dist (priority_encoder_2_out), .out(shifter_8_out));
  assign bit_extender_16_out = {{15{1'b0}}, comparator_12_gt};  // Bit_Extender bit_extender_16
  Shifter #(.width(16)) shifter_9 (.in(bit_extender_16_out), .\dist (priority_encoder_2_out), .out(shifter_9_out));
  Shifter #(.width(16)) shifter_10 (.in(16'h1), .\dist (bit_extender_14_out), .out(shifter_10_out));
  Shifter #(.width(16)) shifter_11 (.in(bit_extender_15_out), .\dist (bit_extender_14_out), .out(shifter_11_out));
  assign and_8_out = not_5_out & Arduino_mode_q;  // AND_Gate and_8, 16 bits wide
  Register #(.width(1)) register_4 (.D(comparator_13_gt), .en(decoder_5_out11), .clk(clk), .Q(uart_en));  // open: clr
  Comparator #(.mode("unsigned")) comparator_13 (.a(data), .b({8{1'b0}}), .gt(comparator_13_gt));  // open: eq, lt
  Register u_A (.D(data), .en(or_10_out), .clk(clk), .Q(A));  // open: clr
  or or_10 (or_10_out, decoder_6_out0, decoder_7_out0);
  Register u_B (.D(data), .en(decoder_7_out1), .clk(clk), .Q(B));  // open: clr
  Register u_H (.D(data), .en(or_11_out), .clk(clk), .Q(H));  // open: clr
  or or_11 (or_11_out, decoder_7_out2, decoder_6_out2);
  Register u_L (.D(data), .en(or_12_out), .clk(clk), .Q(L));  // open: clr
  or or_12 (or_12_out, decoder_7_out3, decoder_6_out3);
  Register u_C0 (.D(data), .en(decoder_6_out4), .clk(clk), .Q(C0));  // open: clr
  Register u_C1 (.D(data), .en(decoder_6_out5), .clk(clk), .Q(C1));  // open: clr
  Register #(.width(4)) register_5 (.D(data[3:0]), .en(decoder_2_out5), .clk(clk), .Q(seven_seg[15:12]));  // open: clr
  assign and_9_out = not_6_out & GPIO_out_q;  // AND_Gate and_9, 36 bits wide
  Register #(.width(36)) GPIO_out (.D(or_13_out), .en(or_6_out), .clk(clk), .Q(GPIO_out_q));  // open: clr
  assign or_13_out = and_9_out | shifter_5_out;  // OR_Gate or_13, 36 bits wide
  assign not_4_out = ~shifter_6_out;  // NOT_Gate not_4, 36 bits wide
  Register #(.width(36)) GPIO_mode (.D(or_14_out), .en(or_7_out), .clk(clk), .Q(GPIO_mode_q));  // open: clr
  assign or_14_out = shifter_7_out | and_7_out;  // OR_Gate or_14, 36 bits wide
  Register #(.width(16)) Arduino_out (
    .D(or_15_out), .en(priority_encoder_2_gs), .clk(clk), .Q(Arduino_out_q));  // open: clr
  assign or_15_out = and_10_out | shifter_9_out;  // OR_Gate or_15, 16 bits wide
  assign not_5_out = ~shifter_10_out;  // NOT_Gate not_5, 16 bits wide
  Register #(.width(16)) Arduino_mode (.D(or_16_out), .en(or_8_out), .clk(clk), .Q(Arduino_mode_q));  // open: clr
  assign or_16_out = shifter_11_out | and_8_out;  // OR_Gate or_16, 16 bits wide
  assign mem_val = mem_write ? data : 8'bz;  // Controlled_Buffer controlled_buffer_1
  Register #(.width(4)) register_6 (.D(data[3:0]), .en(decoder_2_out6), .clk(clk), .Q(seven_seg[19:16]));  // open: clr
  assign not_6_out = ~shifter_4_out;  // NOT_Gate not_6, 36 bits wide
  // PortIO GPIO_port: pin names not known; wires that end beside it: GPIO_mode_q, GPIO_out_q, GPIO_in
  assign not_7_out = ~shifter_8_out;  // NOT_Gate not_7, 16 bits wide
  assign and_10_out = not_7_out & Arduino_out_q;  // AND_Gate and_10, 16 bits wide
  // PortIO Arduino_port: pin names not known; wires that end beside it: Arduino_mode_q, Arduino_port_p2, Arduino_in
  Multiplexer #(.enable("false"), .select(2), .width(8)) multiplexer_19 (
    .in0(A), .in1(B), .in2(H), .in3(L), .out(multiplexer_19_out), .sel(cond));
  Register #(.width(4)) register_7 (.D(data[3:0]), .en(decoder_2_out7), .clk(clk), .Q(seven_seg[23:20]));  // open: clr
  Register graphics_x (.D(data), .en(decoder_2_out30), .clk(clk), .Q(gfx_x));  // open: clr
  assign not_8_out = ~shifter_12_out;  // NOT_Gate not_8, 16 bits wide
  assign and_11_out = shifter_12_out & shifter_15_out;  // AND_Gate and_11, 16 bits wide
  assign not_9_out = ~shifter_16_out;  // NOT_Gate not_9, 16 bits wide
  assign and_12_out = shifter_16_out & shifter_17_out;  // AND_Gate and_12, 16 bits wide
  assign not_10_out = ~pwm_en_q;  // NOT_Gate not_10, 16 bits wide
  assign and_13_out = {4'b0000, PWM_driver_0_modulated[11:9], 2'b00, PWM_driver_0_modulated[6:5], 1'b0, PWM_driver_0_modulated[3], 3'b000} & pwm_en_q;  // AND_Gate and_13, 16 bits wide
  assign and_14_out = Arduino_out_q & not_8_out & not_9_out & not_10_out;  // AND_Gate and_14, 16 bits wide
  assign Arduino_port_p2 = and_14_out | and_11_out | and_12_out | and_13_out;  // OR_Gate or_17, 16 bits wide
  Register #(.width(3)) u_timer_mode_0 (.D(data[2:0]), .en(decoder_5_out12), .clk(clk), .Q(timer_mode_0));  // open: clr
  Register u_timer_count_0 (.D(data), .en(decoder_5_out14), .clk(clk), .Q(timer_count_0));  // open: clr
  Register #(.width(3)) u_timer_mode_1 (.D(data[2:0]), .en(decoder_5_out13), .clk(clk), .Q(timer_mode_1));  // open: clr
  Register u_timer_count_1 (.D(data), .en(decoder_5_out15), .clk(clk), .Q(timer_count_1));  // open: clr
  Multiplexer #(.enable("false"), .select(4), .width(8)) multiplexer_20 (
    .in0(A), .in1(multiplexer_19_out), .in2(H), .in3(L), .in4(C0), .in5(C1), .in6(mem), .in7(PC[7:0]),
    .in8(PC[15:8]), .in9(port_in), .in10(8'hee), .in11(8'hee), .in12(8'hee), .in13(8'hee), .in14(8'hee),
    .in15(8'hee), .out(multiplexer_20_out), .sel(read_sel));
  // Probe on multiplexer_20_out
  Register graphics_y (.D(data), .en(decoder_2_out31), .clk(clk), .Q(gfx_y));  // open: clr
  Bit_Extender #(.out_width(4), .\type ("zero")) bit_extender_17 (.in(data), .out(bit_extender_17_out));
  assign bit_extender_18_out = {{15{1'b0}}, decoder_5_out3};  // Bit_Extender bit_extender_18
  or or_18 (or_18_out, decoder_5_out3, decoder_5_out4);
  Adder adder_11 (.a(multiplexer_20_out), .b(8'h1), .out(adder_11_out), .cout(adder_11_cout[2]));  // open: cin
  Subtractor subtractor_4 (
    .a(multiplexer_20_out), .b(8'h1), .out(subtractor_4_out), .bout(subtractor_4_bout[2]));  // open: bin
  assign bit_extender_19_out = {{15{1'b0}}, ws2812_en};  // Bit_Extender bit_extender_19
  Shifter #(.width(16)) shifter_12 (.in(bit_extender_19_out), .\dist (4'b0001), .out(shifter_12_out));
  assign not_11_out = ~shifter_13_out;  // NOT_Gate not_11, 16 bits wide
  Shifter #(.width(16)) shifter_13 (.in(16'h1), .\dist (bit_extender_17_out), .out(shifter_13_out));
  Shifter #(.width(16)) shifter_14 (.in(bit_extender_18_out), .\dist (bit_extender_17_out), .out(shifter_14_out));
  assign or_19_out = shifter_14_out | and_15_out;  // OR_Gate or_19, 16 bits wide
  assign and_15_out = not_11_out & pwm_en_q;  // AND_Gate and_15, 16 bits wide
  assign bit_extender_20_out = {{15{1'b0}}, ws2812};  // Bit_Extender bit_extender_20
  Shifter #(.width(16)) shifter_15 (.in(bit_extender_20_out), .\dist (4'b0001), .out(shifter_15_out));
  Register #(.width(16)) pwm_en (.D(and_16_out), .en(or_18_out), .clk(clk), .Q(pwm_en_q));  // open: clr
  assign and_16_out = 16'he68 & or_19_out;  // AND_Gate and_16, 16 bits wide
  alu alu_1 (
    .mode(mode), .A(A), .operand(multiplexer_20_out), .flags_in(F), .result(alu_1_result),
    .flags_out(alu_1_flags_out));
  assign bit_extender_21_out = {{15{1'b0}}, uart_en};  // Bit_Extender bit_extender_21
  Shifter #(.width(16)) shifter_16 (.in(bit_extender_21_out), .\dist (4'b0001), .out(shifter_16_out));
  timer timer_0 (
    .mode(timer_mode_0), .count(timer_count_0), .clk(DE10_clk), .reset(decoder_5_out16),
    .triggered(timer_out_0));
  timer timer_1 (
    .mode(timer_mode_1), .count(timer_count_1), .clk(DE10_clk), .reset(decoder_5_out17),
    .triggered(timer_out_1));
  Comparator #(.mode("unsigned")) comparator_14 (.a(data), .b({8{1'b0}}), .eq(adder_11_cout[3]));  // open: gt, lt
  assign bit_extender_22_out = {{15{1'b0}}, tx};  // Bit_Extender bit_extender_22
  Shifter #(.width(16)) shifter_17 (.in(bit_extender_22_out), .\dist (4'b0001), .out(shifter_17_out));
  Multiplexer #(.enable("false"), .select(2), .width(4)) multiplexer_21 (
    .in0(alu_1_flags_out), .in1(multiplexer_23_out), .in2({adder_11_cout, F[1:0]}),
    .in3({adder_11_cout[3], subtractor_4_bout[2], F[1:0]}), .out(F_val), .sel(write_op_sel));
  Register PWM_3 (.D(data), .en(decoder_5_out5), .clk(clk), .Q(PWM_3_q));  // open: clr
  Register PWM_5 (.D(data), .en(decoder_5_out6), .clk(clk), .Q(PWM_5_q));  // open: clr
  Register PWM_6 (.D(data), .en(decoder_5_out7), .clk(clk), .Q(PWM_6_q));  // open: clr
  Register PWM_9 (.D(data), .en(decoder_5_out8), .clk(clk), .Q(PWM_9_q));  // open: clr
  Register PWM_10 (.D(data), .en(decoder_5_out9), .clk(clk), .Q(PWM_10_q));  // open: clr
  Register PWM_11 (.D(data), .en(decoder_5_out10), .clk(clk), .Q(PWM_11_q));  // open: clr
  Multiplexer #(.enable("false"), .select(2), .width(8)) multiplexer_22 (
    .in0(alu_1_result), .in1(multiplexer_20_out), .in2(adder_11_out), .in3(subtractor_4_out), .out(data),
    .sel(write_op_sel));
  Negator negator_1 (.in(SP), .out(negator_1_out));
  Comparator comparator_15 (.a(data), .b({8{1'b0}}), .eq(comparator_15_eq));  // open: gt, lt
  // Probe on data
  assign bit_extender_23_out = {{8{1'b1}}, negator_1_out};  // Bit_Extender bit_extender_23
  Comparator #(.mode("unsigned"), .width(16)) comparator_16 (
    .a(PC), .b({16{1'b0}}), .gt(comparator_16_gt));  // open: eq, lt
  assign and_17_out = F & 4'b0111;  // AND_Gate and_17, 4 bits wide
  Multiplexer #(.enable("false"), .width(4)) multiplexer_23 (
    .in0(and_17_out), .in1(or_20_out), .out(multiplexer_23_out), .sel(comparator_15_eq));
  assign or_20_out = F | 4'b1000;  // OR_Gate or_20, 4 bits wide
  Multiplexer #(.enable("false"), .select(2), .width(16)) multiplexer_24 (
    .in0(PC), .in1(bit_extender_23_out), .in2({H, L}), .in3({C0, C1}), .out(multiplexer_24_out),
    .sel(addr_mode));
  Multiplexer #(.enable("false"), .width(16)) multiplexer_25 (
    .in0(multiplexer_24_out), .in1(addr_override), .out(multiplexer_25_out), .sel(and_18_out));
  and and_18 (and_18_out, addr_override_en, comparator_16_gt);
  PWM_driver PWM_driver_0 (.clk(clk), .duty_cycle(PWM_3_q), .modulated(PWM_driver_0_modulated[3]));
  PWM_driver PWM_driver_1 (.clk(clk), .duty_cycle(PWM_5_q), .modulated(PWM_driver_0_modulated[5]));
  PWM_driver PWM_driver_2 (.clk(clk), .duty_cycle(PWM_6_q), .modulated(PWM_driver_0_modulated[6]));
  PWM_driver PWM_driver_3 (.clk(clk), .duty_cycle(PWM_9_q), .modulated(PWM_driver_0_modulated[9]));
  PWM_driver PWM_driver_4 (.clk(clk), .duty_cycle(PWM_10_q), .modulated(PWM_driver_0_modulated[10]));
  PWM_driver PWM_driver_5 (.clk(clk), .duty_cycle(PWM_11_q), .modulated(PWM_driver_0_modulated[11]));
  // Probe on multiplexer_25_out
  RAM #(.addrWidth(15)) RAM_1 (
    .addr(multiplexer_25_out[14:0]), .we(mem_write), .oe(1'b1), .clk(clk), .din(mem_val), .dout(RAM_1_dout));
  ROM #(.addrWidth(15)) Program (.addr(multiplexer_25_out[14:0]), .data(Program_data));
  Subtractor #(.width(5)) subtractor_5 (.a(C0[4:0]), .b(5'b00010), .out(subtractor_5_out));  // open: bin, bout
  Subtractor #(.width(5)) subtractor_6 (.a(C0[4:0]), .b(5'b01010), .out(subtractor_6_out));  // open: bin, bout
  Subtractor #(.width(5)) subtractor_7 (.a(C0[4:0]), .b(5'b10100), .out(subtractor_7_out));  // open: bin, bout
  Subtractor subtractor_8 (.a(C0), .b(8'h23), .out(subtractor_8_out));  // open: bin, bout
  Subtractor #(.width(5)) subtractor_9 (.a(C0[4:0]), .b(5'b00111), .out(subtractor_9_out));  // open: bin, bout
  Random random_1 (.next(1'b1), .clk(clock_2_out), .out(random_1_out));  // open: clr
  Clock clock_2 (.out(clock_2_out));
  assign bit_extender_24_out = {{4{1'b0}}, multiplexer_26_out};  // Bit_Extender bit_extender_24
  Multiplexer #(.enable("false"), .select(3), .width(4)) multiplexer_26 (
    .in0(seven_seg[3:0]), .in1(seven_seg[7:4]), .in2(seven_seg[11:8]), .in3(seven_seg[15:12]),
    .in4(seven_seg[19:16]), .in5(seven_seg[23:20]), .out(multiplexer_26_out), .sel(subtractor_5_out[2:0]));  // open: in6, in7
  Shifter #(.width(10)) shifter_18 (.in(10'h1), .\dist (subtractor_6_out[3:0]), .out(shifter_18_out));
  Shifter #(.width(10)) shifter_19 (.in(10'h1), .\dist (subtractor_7_out[3:0]), .out(shifter_19_out));
  Shifter #(.width(36)) shifter_20 (.in(36'h1), .\dist (subtractor_8_out[5:0]), .out(shifter_20_out));
  Shifter #(.width(16)) shifter_21 (.in(16'h1), .\dist (subtractor_9_out[3:0]), .out(shifter_21_out));
  assign bit_extender_25_out = {{5{1'b0}}, timer_mode_0};  // Bit_Extender bit_extender_25
  assign bit_extender_26_out = {{5{1'b0}}, timer_mode_1};  // Bit_Extender bit_extender_26
  assign bit_extender_27_out = {{7{1'b0}}, timer_out_0};  // Bit_Extender bit_extender_27
  assign bit_extender_28_out = {{7{1'b0}}, timer_out_1};  // Bit_Extender bit_extender_28
  assign and_19_out = shifter_18_out & leds;  // AND_Gate and_19, 10 bits wide
  Comparator #(.mode("unsigned"), .width(10)) comparator_17 (
    .a(and_19_out), .b({10{1'b0}}), .gt(comparator_17_gt));  // open: eq, lt
  assign and_20_out = shifter_19_out & switches;  // AND_Gate and_20, 10 bits wide
  Comparator #(.mode("unsigned"), .width(10)) comparator_18 (
    .a(and_20_out), .b({10{1'b0}}), .gt(comparator_18_gt));  // open: eq, lt
  assign and_21_out = shifter_20_out & GPIO_in;  // AND_Gate and_21, 36 bits wide
  Comparator #(.mode("unsigned"), .width(36)) comparator_19 (
    .a(and_21_out), .b({36{1'b0}}), .gt(comparator_19_gt));  // open: eq, lt
  assign and_22_out = shifter_21_out & Arduino_in;  // AND_Gate and_22, 16 bits wide
  Comparator #(.mode("unsigned"), .width(16)) comparator_20 (
    .a(and_22_out), .b({16{1'b0}}), .gt(comparator_20_gt));  // open: eq, lt
  assign bit_extender_29_out = {{7{1'b0}}, btn0};  // Bit_Extender bit_extender_29
  assign bit_extender_30_out = {{7{1'b0}}, btn1};  // Bit_Extender bit_extender_30
  assign bit_extender_31_out = {{7{1'b0}}, comparator_17_gt};  // Bit_Extender bit_extender_31
  assign bit_extender_32_out = {{7{1'b0}}, comparator_18_gt};  // Bit_Extender bit_extender_32
  assign bit_extender_33_out = {{7{1'b0}}, comparator_19_gt};  // Bit_Extender bit_extender_33
  assign bit_extender_34_out = {{7{1'b0}}, comparator_20_gt};  // Bit_Extender bit_extender_34
  assign bit_extender_35_out = {{7{1'b0}}, uart_en};  // Bit_Extender bit_extender_35
  // Probe on mem
  Multiplexer #(.enable("false"), .width(8)) multiplexer_27 (
    .in0(Program_data), .in1(RAM_1_dout), .out(mem), .sel(multiplexer_25_out[15]));
  Multiplexer #(.enable("false"), .select(5), .width(8)) multiplexer_28 (
    .in0(uart_in), .in1(uart_available), .in2(bit_extender_24_out), .in3(bit_extender_24_out),
    .in4(bit_extender_24_out), .in5(bit_extender_24_out), .in6(bit_extender_24_out),
    .in7(bit_extender_24_out), .in8(bit_extender_29_out), .in9(bit_extender_30_out),
    .in10(bit_extender_31_out), .in11(bit_extender_31_out), .in12(bit_extender_31_out),
    .in13(bit_extender_31_out), .in14(bit_extender_31_out), .in15(bit_extender_31_out),
    .in16(bit_extender_31_out), .in17(bit_extender_31_out), .in18(bit_extender_31_out),
    .in19(bit_extender_31_out), .in20(bit_extender_32_out), .in21(bit_extender_32_out),
    .in22(bit_extender_32_out), .in23(bit_extender_32_out), .in24(bit_extender_32_out),
    .in25(bit_extender_32_out), .in26(bit_extender_32_out), .in27(bit_extender_32_out),
    .in28(bit_extender_32_out), .in29(bit_extender_32_out), .in30(gfx_x), .in31(gfx_y),
    .out(multiplexer_28_out), .sel(C0[4:0]));
  Multiplexer #(.enable("false"), .select(5), .width(8)) multiplexer_29 (
    .in0({8{1'b0}}), .in1({8{1'b0}}), .in2({8{1'b0}}), .in3(bit_extender_33_out), .in4(bit_extender_33_out),
    .in5(bit_extender_33_out), .in6(bit_extender_33_out), .in7(bit_extender_33_out),
    .in8(bit_extender_33_out), .in9(bit_extender_33_out), .in10(bit_extender_33_out),
    .in11(bit_extender_33_out), .in12(bit_extender_33_out), .in13(bit_extender_33_out),
    .in14(bit_extender_33_out), .in15(bit_extender_33_out), .in16(bit_extender_33_out),
    .in17(bit_extender_33_out), .in18(bit_extender_33_out), .in19(bit_extender_33_out),
    .in20(bit_extender_33_out), .in21(bit_extender_33_out), .in22(bit_extender_33_out),
    .in23(bit_extender_33_out), .in24(bit_extender_33_out), .in25(bit_extender_33_out),
    .in26(bit_extender_33_out), .in27(bit_extender_33_out), .in28(bit_extender_33_out),
    .in29(bit_extender_33_out), .in30(bit_extender_33_out), .in31(bit_extender_33_out),
    .out(multiplexer_29_out), .sel(C0[4:0]));
  Multiplexer #(.enable("false"), .select(5), .width(8)) multiplexer_30 (
    .in0(bit_extender_33_out), .in1(bit_extender_33_out), .in2(bit_extender_33_out),
    .in3(bit_extender_33_out), .in4(bit_extender_33_out), .in5(bit_extender_33_out),
    .in6(bit_extender_33_out), .in7(bit_extender_34_out), .in8(bit_extender_34_out),
    .in9(bit_extender_34_out), .in10(bit_extender_34_out), .in11(bit_extender_34_out),
    .in12(bit_extender_34_out), .in13(bit_extender_34_out), .in14(bit_extender_34_out),
    .in15(bit_extender_34_out), .in16(bit_extender_34_out), .in17(bit_extender_34_out),
    .in18(bit_extender_34_out), .in19(bit_extender_34_out), .in20(bit_extender_34_out),
    .in21(bit_extender_34_out), .in22(bit_extender_34_out), .in23(adc_0), .in24(adc_1), .in25(adc_2),
    .in26(adc_3), .in27(adc_4), .in28(adc_5), .in29(random_1_out), .in30({8{1'b0}}), .in31({8{1'b0}}),
    .out(multiplexer_30_out), .sel(C0[4:0]));
  Multiplexer #(.enable("false"), .select(5), .width(8)) multiplexer_31 (
    .in0({8{1'b0}}), .in1({8{1'b0}}), .in2({8{1'b0}}), .in3({8{1'b0}}), .in4({8{1'b0}}), .in5({8{1'b0}}),
    .in6({8{1'b0}}), .in7({8{1'b0}}), .in8({8{1'b0}}), .in9({8{1'b0}}), .in10({8{1'b0}}),
    .in11(bit_extender_35_out), .in12(bit_extender_25_out), .in13(bit_extender_26_out), .in14(timer_count_0),
    .in15(timer_count_1), .in16(bit_extender_27_out), .in17(bit_extender_28_out), .in18({8{1'b0}}),
    .in19({8{1'b0}}), .in20({8{1'b0}}), .in21({8{1'b0}}), .in22({8{1'b0}}), .in23({8{1'b0}}),
    .in24({8{1'b0}}), .in25({8{1'b0}}), .in26({8{1'b0}}), .in27({8{1'b0}}), .in28({8{1'b0}}),
    .in29({8{1'b0}}), .in30({8{1'b0}}), .in31({8{1'b0}}), .out(multiplexer_31_out), .sel(C0[4:0]));
  // Probe on C0[4:0]
  // Probe on C0[6:5]
  Multiplexer #(.enable("false"), .select(2), .width(8)) multiplexer_32 (
    .in0(multiplexer_28_out), .in1(multiplexer_29_out), .in2(multiplexer_30_out), .in3(multiplexer_31_out),
    .out(port_in), .sel(C0[6:5]));
  // Probe on port_in

  // Other names for the same wires on the sheet: mode_1 = mode[0]; mode_2[1:0] = mode[1:0];
  //   draw_sprite_freeze = addr_override_en; instr[1:0] = cond; reg_sel[1:0] = cond

  // Notes on the sheet:
  //   2 pins
  //   TTY
  //   UART
  //   contents of Microcode (hex, n*v repeats v):
  //   800000 9*0 a60164 7*0 220464 0 220564 3 860167 0 0 2 860166 7*0 220464 0 220564 820617 0 0 0 820616
  //   8*0 220264 0 a20364 5*0 220464 860194 6*0 220464 820714 4*0 860118 7*0 86011c 7*0 60338 81034 860228
  //   5*0 6033c 81834 86022c 7*0 220464 860040 4*0 860010 9*0 220464 860840 4*0 860810 9*0 220464 861040
  //   4*0 861010 9*0 220464 861840 4*0 861810 9*0 220464 862040 4*0 862010 9*0 220464 862840 4*0 862810
  //   9*0 220464 863040 4*0 863010 9*0 220464 843840 4*0 843810 9*0 220464 0 220564 c00800 0 0 c00000 9*0
  //   401064 a00000 6*0 220464 80800 c01044 5*0 220464 80000 c01044 4*0 20404 860194 6*0 20404 820714 5*0
  //   8000 820615 7*0 1 838165 7*0 220464 0 228564 28675 20685 c00800 0 1 38465 1 38565 c00800 0 0 0
  //   100000 6*0 864010 7*0 864810 7*0 865010
  //   ADC Driver
  //   VGA Driver
  //   RGB Video 160x128 8-bit color
  //   14 pins
  //   36 pins (per-bit)
  //   16 pins (per-bit)
  //   contents of Program (hex, n*v repeats v):
  //   4 5 20 6c 4 2 20 6e 74 2 cc 71 81 3 49 7c fa 9c 92 6 0 71 81 4 49 26 7c f9 92 94 96 9c 92 91 90 96 4
  //   0 71 80 4 3a 29 7c fa 95 96 9c 90 91 18 0 0 6c 0 80 d 90 93 94 39 90 97 85 1 26 94 28 7c f1 95 94 9c
  //   90 3b 85 1 26 90 97 94 9c 90 91 92 93 72 81 b 84 c 90 91 94 73 94 81 2 7c 3 74 0 e4 90 91 92 93 90
  //   91 92 93 95 94 97 96 98 1 45 92 94 6c 0 97 96 95 94 82 58 6c 0 86 16 90 92 94 6c 0 94 86 e 90 4 80
  //   10 80 3 4 80 10 80 4 94 7c c 90 4 0 10 80 3 4 0 10 80 4 94 90 91 92 93 90 91 92 93 95 94 97 96 98 1
  //   45 90 92 94 6c 0 94 84 e 90 93 94 6c 0 94 84 6 97 96 95 94 7c 60 97 96 95 94 8 80 3 24 10 80 3 7c 53
  //   4 80 10 80 3 4 0 10 80 4 7c 47 90 91 92 93 90 91 92 93 95 94 97 96 98 1 45 92 94 6c 0 97 96 95 94 82
  //   c 4 0 10 80 3 4 c0 10 80 4 7c 22 6c 0 82 14 90 92 94 6c 0 94 82 c 4 fe 10 80 3 4 ff 10 80 4 7c a 4
  //   7f 10 80 3 4 80 10 80 4 8 80 3 9 80 4 71 97 96 95 94 9c 90 3a 90 96 91 94 3b 90 97 85 1 26 94 9c 90
  //   90 92 94 96 4a 90 96 93 94 49 90 97 85 1 2a 94 9c 93 2b 81 11 90 91 94 a4 90 95 94 81 3 a4 7c f1 a4
  //   5c 1 7c ec 97 9c 93 2b 81 17 a8 81 9 90 91 94 a8 90 95 94 7c f1 90 91 94 a8 5c 80 90 95 94 7c e6 97
  //   9c 90 91 54 80 90 92 94 54 80 90 95 94 69 10 80 2 95 92 94 54 80 80 d 92 94 64 ff 90 96 93 94 64 ff
  //   90 97 2c 94 90 54 80 94 80 13 92 93 64 ff 90 91 94 64 ff 90 97 96 2c 92 94 93 95 97 96 9c 90 91 92
  //   94 9 80 2 61 90 96 95 94 9c 90 4 0 10 80 0 10 80 1 94 92 93 a 80 0 b 80 1 98 1 37 12 80 0 13 80 1 97
  //   96 30 90 4 0 72 94 84 e5 90 4 0 73 94 84 de a 80 0 b 80 1 9c 98 1 8b 98 1 d7 98 1 ca 9c 90 91 90 4 0
  //   10 80 0 10 80 1 94 98 0 52 81 22 90 91 92 93 95 94 97 96 98 1 45 90 91 92 93 95 94 a 80 0 b 80 1 2c
  //   12 80 0 13 80 1 97 96 7c d9 95 94 a 80 0 b 80 1 9c 98 1 8b 98 2 14 98 1 ca 9c 90 91 98 0 52 81 15 90
  //   91 92 93 95 94 97 96 98 1 45 90 91 92 93 95 94 97 96 7c e6 90 96 91 97 95 94 9c 90 91 90 91 98 1 8b
  //   98 2 5a 95 94 54 80 90 92 94 54 80 90 95 94 69 80 d 92 94 64 ff 90 96 93 94 64 ff 90 97 2c 95 94 9c
  //   98 3 3d 98 4 f0 98 4 aa 80 3 74 2 cc 98 4 cf 8 80 11 10 80 a 8 80 10 10 80 9 98 4 1 98 3 4e 74 2 a6
  //   4 25 20 22 18 6 3f 5 32 91 c 2c 5 8 98 0 20 20 1e c 2c 98 0 20 20 1f 92 93 18 5 bf 20 21 97 96 95 29
  //   84 e2 4 18 20 1e 4 10 20 1f 92 93 18 5 7f 20 21 97 96 4 78 20 1e 4 18 20 1f 92 93 18 5 ff 20 21 97
  //   96 20 5e 98 5 59 84 fb 98 5 59 80 fb 4 20 10 80 9 10 80 a 4 2 10 80 5 18 80 12 14 2c 14 98 4 60 98 3
  //   4e 74 2 a6 90 20 70 98 5 59 80 3 10 80 6 1c 70 80 f4 94 9c 90 4 25 20 22 98 3 60 98 3 76 98 3 ca 20
  //   5e 94 9c 90 8 80 7 20 1e 8 80 8 20 1f 92 93 18 5 ff 20 21 97 96 94 9c 90 8 80 9 20 1e 8 80 a 20 1f
  //   92 93 18 5 7f 20 21 97 96 94 9c 90 c 92 93 a 80 b b 80 c 6c 0 84 8 92 94 34 8 90 96 7c 1e 6c 1 84 8
  //   93 94 34 8 90 97 7c 12 6c 2 84 8 92 94 44 8 90 96 7c 6 93 94 44 8 90 97 12 80 b 13 80 c 97 96 94 9c
  //   90 91 92 93 8 80 9 10 80 b 8 80 a 10 80 c 18 80 12 9 80 5 80 1a 98 3 8c 8 80 b 20 1e 8 80 c 20 1f 92
  //   93 18 5 bf 20 21 97 96 2c 29 7c e4 97 96 95 94 9c 90 91 92 93 18 80 12 9 80 5 80 e c 90 8 80 d 14 2c
  //   94 10 80 d 29 7c f0 97 96 95 94 9c 90 91 92 93 8 80 9 10 80 b 8 80 a 10 80 c 18 80 12 9 80 5 91 8 80
  //   e 9 80 b 71 84 11 8 80 f 9 80 c 71 84 8 95 97 96 95 94 4 1 9c 95 98 3 8c 2c 29 85 dd 97 96 95 94 4 0
  //   9c 90 91 92 5 8 1c 5d 54 f 90 96 1c 5d 54 3 3a 90 96 1c 5d 54 1 3a 98 0 20 90 96 1c 5d 54 f 98 0 20
  //   9 80 11 71 84 a 90 8 80 10 72 94 84 2 7c d0 12 80 e 10 80 f 90 98 4 20 94 84 c3 12 80 7 10 80 8 96
  //   95 94 9c 8 80 10 6c a0 85 1b 8 80 11 6c 80 85 14 8 80 10 10 80 e 8 80 11 10 80 f 98 4 20 84 3 4 0 9c
  //   4 1 9c 90 91 8 80 10 9 80 7 71 84 13 8 80 11 9 80 8 71 84 a 8 80 5 24 10 80 5 98 4 60 95 94 9c 90 91
  //   8 80 6 80 7 28 9 80 12 71 84 6 8 80 12 98 5 75 90 6c 0 84 10 8 80 9 34 8 10 80 10 8 80 a 10 80 11 7c
  //   36 6c 1 84 10 8 80 9 10 80 10 8 80 a 34 8 10 80 11 7c 22 6c 2 84 10 8 80 9 44 8 10 80 10 8 80 a 10
  //   80 11 7c e 8 80 9 10 80 10 8 80 a 44 8 10 80 11 94 98 5 75 10 80 d 95 94 9c 1c 26 80 3 4 1 9c 1c 24
  //   80 3 4 2 9c 1c 25 80 3 4 3 9c 1c 23 80 2 4 4 9c 91 5 4 34 2 98 0 b 95 9c 9*c 6*38 c c 38 0 38 38 0
  //   38 c c 38 38 38 e0 38 38 c c 38 38 38 e0 38 38 c c 38 38 38 e0 38 38 c c 38 38 e0 38 e0 38 18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
endmodule

module alu (
  input  [3:0] mode,
  input  [7:0] A,
  input  [7:0] operand,
  input  [3:0] flags_in,
  output [7:0] result,
  output [3:0] flags_out
);

  wire adder_1_cout, adder_2_cout, comparator_1_lt, comparator_2_lt, subtractor_1_bout, subtractor_2_bout,
       xnor_1_out, xor_2_out;
  wire [1:0] and_2_out;
  wire [7:0] adder_1_out, adder_2_out, and_1_out, or_1_out, shifter_1_out, shifter_2_out, shifter_3_out,
       subtractor_1_out, subtractor_2_out, xor_1_out;

  Comparator comparator_1 (.a(A), .b({8{1'b0}}), .lt(comparator_1_lt));  // open: gt, eq
  Comparator comparator_2 (.a(operand), .b({8{1'b0}}), .lt(comparator_2_lt));  // open: gt, eq
  Adder adder_1 (.a(A), .b(operand), .out(adder_1_out), .cout(adder_1_cout));  // open: cin
  Adder adder_2 (.a(A), .b(operand), .out(adder_2_out), .cin(flags_in[2]), .cout(adder_2_cout));
  Subtractor subtractor_1 (.a(A), .b(operand), .out(subtractor_1_out), .bout(subtractor_1_bout));  // open: bin
  Subtractor subtractor_2 (.a(A), .b(operand), .out(subtractor_2_out), .bin(flags_in[2]), .bout(subtractor_2_bout));
  assign and_1_out = A & operand;  // AND_Gate and_1, 8 bits wide
  assign or_1_out = A | operand;  // OR_Gate or_1, 8 bits wide
  assign xor_1_out = A ^ operand;  // XOR_Gate xor_1, 8 bits wide
  Shifter shifter_1 (.in(A), .\dist (3'b001), .out(shifter_1_out));
  Shifter #(.shift("lr")) shifter_2 (.in(A), .\dist (3'b001), .out(shifter_2_out));
  Shifter #(.shift("ar")) shifter_3 (.in(A), .\dist (3'b001), .out(shifter_3_out));
  xnor xnor_1 (xnor_1_out, comparator_1_lt, comparator_2_lt);
  and and_2 (and_2_out[0], xnor_1_out, xor_2_out);
  Multiplexer #(.enable("false"), .select(4), .width(2)) multiplexer_1 (
    .in0(and_2_out), .in1(and_2_out), .in2(and_2_out), .in3(and_2_out), .in4(flags_in[1:0]),
    .in5(flags_in[1:0]), .in6(flags_in[1:0]), .in7(and_2_out), .in8(flags_in[1:0]), .in9(flags_in[1:0]),
    .in10(flags_in[1:0]), .in11(flags_in[1:0]), .in12(flags_in[1:0]), .in13(flags_in[1:0]),
    .in14(flags_in[1:0]), .in15(flags_in[1:0]), .out(flags_out[1:0]), .sel(mode));
  Multiplexer #(.enable("false"), .select(4)) multiplexer_2 (
    .in0(adder_1_cout), .in1(adder_2_cout), .in2(subtractor_1_bout), .in3(subtractor_2_bout),
    .in4(flags_in[2]), .in5(flags_in[2]), .in6(flags_in[2]), .in7(subtractor_1_bout), .in8(A[7]), .in9(A[0]),
    .in10(A[0]), .in11(flags_in[2]), .in12(flags_in[2]), .in13(flags_in[2]), .in14(flags_in[2]),
    .in15(flags_in[2]), .out(flags_out[2]), .sel(mode));
  xor xor_2 (xor_2_out, comparator_2_lt, and_2_out[1]);
  Comparator comparator_3 (.a(result), .b({8{1'b0}}), .eq(flags_out[3]), .lt(and_2_out[1]));  // open: gt
  Multiplexer #(.enable("false"), .select(4), .width(8)) multiplexer_3 (
    .in0(adder_1_out), .in1(adder_2_out), .in2(subtractor_1_out), .in3(subtractor_2_out), .in4(and_1_out),
    .in5(or_1_out), .in6(xor_1_out), .in7(subtractor_1_out), .in8(shifter_1_out), .in9(shifter_2_out),
    .in10(shifter_3_out), .in11(8'hee), .in12(8'hee), .in13(8'hee), .in14(8'hee), .in15(8'hee), .out(result),
    .sel(mode));

  // Notes on the sheet:
  //   ADD
  //   ADC
  //   SUB
  //   SBC
  //   AND
  //   OR
  //   LSL
  //   LSR
  //   XOR
  //   ASR
endmodule

module PWM_driver (
  input  clk,
  input  [7:0] duty_cycle,
  output modulated
);

  wire comparator_1_lt, comparator_2_eq;
  wire [7:0] adder_1_out, register_1_q;

  Register register_1 (.D(adder_1_out), .en(1'b1), .clk(clk), .Q(register_1_q));  // open: clr
  Comparator #(.mode("unsigned")) comparator_1 (.a(adder_1_out), .b(duty_cycle), .lt(comparator_1_lt));  // open: gt, eq
  Comparator #(.mode("unsigned")) comparator_2 (.a(duty_cycle), .b({8{1'b1}}), .eq(comparator_2_eq));  // open: gt, lt
  Adder adder_1 (.a(register_1_q), .b(8'h1), .out(adder_1_out));  // open: cin, cout
  or or_1 (modulated, comparator_1_lt, comparator_2_eq);
endmodule

module timer (
  input  [2:0] mode,
  input  [7:0] count,
  input  clk,
  input  reset,
  output triggered
);

  wire comparator_1_lt;
  wire [36:0] adder_1_out, bit_extender_1_out, multiplexer_1_out, multiplier_1_out, register_1_q;

  assign bit_extender_1_out = {{29{1'b0}}, count};  // Bit_Extender bit_extender_1
  Multiplexer #(.enable("false"), .select(3), .width(37)) multiplexer_1 (
    .in0(37'h32), .in1(37'h1f4), .in2(37'h1388), .in3(37'hc350), .in4(37'h7a120), .in5(37'h4c4b40),
    .in6(37'h2faf080), .in7(37'h1dcd6500), .out(multiplexer_1_out), .sel(mode));
  Register #(.width(37)) register_1 (.D(adder_1_out), .en(comparator_1_lt), .clk(clk), .Q(register_1_q), .clr(reset));
  Multiplier #(.width(37)) multiplier_1 (
    .a(multiplexer_1_out), .b(bit_extender_1_out), .out(multiplier_1_out));  // open: cin, cout
  Comparator #(.mode("unsigned"), .width(37)) comparator_1 (
    .a(register_1_q), .b(multiplier_1_out), .lt(comparator_1_lt));  // open: gt, eq
  Adder #(.width(37)) adder_1 (.a(register_1_q), .b(37'h1), .out(adder_1_out));  // open: cin, cout
  not not_1 (triggered, comparator_1_lt);
endmodule

// VHDL entity DE10_RAM, as the project stores it:
-- A syncronous RAM component compatible with the DE10-Lite board

library ieee;
use ieee.std_logic_1164.all;

entity DE10_RAM is
	port (
  		WE : in std_logic; -- Write enable
  		clk : in std_logic; -- Clock pin
  		DataIn : in std_logic_vector(7 downto 0); -- Data input
  		Address : in std_logic_vector(14 downto 0); -- Memory address
  		DataOut : out std_logic_vector(7 downto 0) -- Data output
	);
end DE10_RAM;

architecture impl of DE10_RAM is
	type MEMORY_ARRAY is array (32767 downto 0) of std_logic_vector(7 downto 0);
	signal memory : MEMORY_ARRAY;
begin
	process (clk, Address, DataIn, WE)
	begin
     	if (clk'event and (clk = '1')) then
     		if (WE = '1') then
          		memory(to_integer(unsigned(Address))) <= DataIn;
          	end if;
			DataOut <= memory(to_integer(unsigned(Address)));
      	end if;
	end process;
end architecture;

// VHDL entity VGA_driver, as the project stores it:
-- A DE10-Lite VGA driver

library ieee;
use ieee.std_logic_1164.all;
use ieee.numeric_std.all;
use ieee.std_logic_unsigned.all;

entity VGA_driver is
	port (
		display_clk : in std_logic; -- The real 50 MHz clock
		swap : in std_logic; -- Swap the display buffers
		color_in : in std_logic_vector(7 downto 0); -- Color of pixel to write into VRAM
		x_in, y_in : in std_logic_vector(7 downto 0); -- Coordinates of pixel to write
		clk : in std_logic; -- Clock for writing to VRAM
		WE : in std_logic; -- VRAM write enable
		HS, VS : out std_logic; -- VGA horizontal and vertical sync
		vga_r, vga_g, vga_b : out std_logic_vector(3 downto 0) -- VGA output color
	);
end VGA_driver;

architecture TypeArchitecture of VGA_driver is
	type COLOR_ARRAY is array (20480 * 2 - 1 downto 0) of std_logic_vector(11 downto 0);
	
	signal h_cnt : unsigned(10 downto 0);
	signal v_cnt : unsigned(9 downto 0);
	signal vga_clk : std_logic;
	signal display_buffer : COLOR_ARRAY;
	signal color : std_logic_vector(11 downto 0);
	signal x : unsigned(10 downto 0);
	signal y : unsigned(9 downto 0);
	signal buffer_index : unsigned(19 downto 0);
	signal buf : std_logic;

	constant double_buffered : std_logic := '1';
begin
	process(display_clk)
	begin
		if display_clk'event and display_clk='1' then
			vga_clk <= not vga_clk;
		end if;
	end process;

	process(clk, swap)
	begin
        if rising_edge(clk) and swap='1' then
            buf <= not buf;
        end if;
	end process;

	process(clk, buf, WE, color_in, x_in, y_in)
		variable r, g, b : unsigned(11 downto 0);
		variable index : integer range 0 to 20480 * 2 - 1;
	begin
		index := to_integer(unsigned(x_in) + unsigned(y_in) * 160);
		if buf='1' and double_buffered='1' then
            index := index + 20480;
		end if;
		if clk'event and clk='0' then
			if WE='1' then
				r := shift_left("000000" & unsigned(color_in(7 downto 5)) * 255 / 7, 8);
				g := shift_left("000000" & unsigned(color_in(4 downto 2)) * 255 / 7, 4);
				b := "00000000" & unsigned(color_in(1 downto 0)) * 255 / 3;
				display_buffer(index) <= std_logic_vector(r or g or b);
			end if;
		end if;
	end process;
	
	process(display_clk, x, y)
		variable data : std_logic_vector(11 downto 0);
	begin
		if display_clk'event and display_clk='1' then
			data := display_buffer(to_integer(buffer_index));
			if x<=159 and y<=127 then
				color <= data;
			else
				color <= x"000";
			end if;
		end if;
	end process;
	
	process(vga_clk, buf, color)
	begin
		if vga_clk'event and vga_clk='1' then
			if h_cnt<784 and h_cnt>=144 + 3 + 80 and v_cnt<514 and v_cnt>=11 then
				vga_r <= color(11 downto 8);
				vga_g <= color(7 downto 4);
				vga_b <= color(3 downto 0);
			else
				vga_r <= x"0";
				vga_g <= x"0";
				vga_b <= x"0";
			end if;
			
			if h_cnt=799 then
				h_cnt <= to_unsigned(0, 11);
				if v_cnt=524 then
					v_cnt <= to_unsigned(0, 10);
				else
					v_cnt <= v_cnt + 1;
				end if;
			else
				h_cnt <= h_cnt + 1;
			end if;
			
			if h_cnt<96 then
				HS <= '1';
			else
				HS <= '0';
			end if;
				
			if v_cnt<2 then
				VS <= '1';
			else
				VS <= '0';
			end if;
					
			x <= (h_cnt - 144 - 80) / 3;
			y <= (v_cnt - 11 - 48) / 3;
			if buf='0' and double_buffered='1' then
                buffer_index <= x + y * 160 + 20480;
            else
                buffer_index <= x + y * 160;
            end if;
		end if;
	end process;
end TypeArchitecture;

// VHDL entity ADC_dummy, as the project stores it:
-- A placeholder ADC component for DE10-Lite

library ieee;
use ieee.std_logic_1164.all;

entity ADC_dummy is
  port (
	  adc_clk : in std_logic;
	  ch0 : out std_logic_vector(7 downto 0);
	  ch1 : out std_logic_vector(7 downto 0);
	  ch2 : out std_logic_vector(7 downto 0);
	  ch3 : out std_logic_vector(7 downto 0);
	  ch4 : out std_logic_vector(7 downto 0);
	  ch5 : out std_logic_vector(7 downto 0)
    );
end ADC_dummy;

architecture stub of ADC_dummy is
begin
end architecture;

// VHDL entity UART_dummy, as the project stores it:
-- A placeholder UART component for DE10-Lite

library ieee;
use ieee.std_logic_1164.all;

entity UART_dummy is
   port (
   	clk : in  std_logic;
  	uart_clk : in  std_logic;
     data : in  std_logic_vector(7 downto 0);
     valid : in  std_logic;
     rx : in  std_logic;
     pop : in std_logic;
     full : out std_logic;
     tx : out std_logic;
     received : out std_logic_vector(7 downto 0);
     available : out std_logic_vector(7 downto 0)
   );
end UART_dummy;

architecture stub of UART_dummy is
begin
end architecture;
