// Digital circuit timer.dig as structural Verilog
module timer (
  input  [7:0] D,
  input  WriteUnit,
  input  WriteCount,
  input  Clear,
  input  Clock,
  output Q
);

  wire comparator_1_gt, or_1_out;
  wire [2:0] Unit_q;
  wire [7:0] Count_q;
  wire [28:0] multiplexer_1_out;
  wire [36:0] add_1_s, multiplexer_2_out, State_q;
  wire [57:0] mul_1_mul;

  or or_1 (or_1_out, Clear, comparator_1_gt);
  Register #(.Bits(3)) Unit (.D(D[2:0]), .C(Clock), .en(WriteUnit), .Q(Unit_q));
  Register #(.Bits(8)) Count (.D(D), .C(Clock), .en(WriteCount), .Q(Count_q));
  Register #(.Bits(37)) State (.D(multiplexer_2_out), .C(Clock), .en(or_1_out), .Q(State_q));
  Multiplexer #(.Bits(29), .Selector_Bits(3)) multiplexer_1 (
    .sel(Unit_q), .in_0(29'h32), .in_1(29'h1f4), .in_2(29'h1388), .in_3(29'hc350), .in_4(29'h7a120),
    .in_5(29'h4c4b40), .in_6(29'h2faf080), .in_7(29'h1dcd6500), .out(multiplexer_1_out));
  Multiplexer #(.Bits(37)) multiplexer_2 (.sel(Clear), .in_0(add_1_s), .in_1({37{1'b0}}), .out(multiplexer_2_out));
  Mul #(.Bits(29)) mul_1 (.a(multiplexer_1_out), .b({{21{1'b0}}, Count_q}), .mul(mul_1_mul));
  Add #(.Bits(37)) add_1 (.a(37'h1), .b(State_q), .c_i(1'b0), .s(add_1_s));  // open: c_o
  Comparator #(.Bits(37)) comparator_1 (.a(mul_1_mul[36:0]), .b(State_q), .gt(comparator_1_gt));  // open: eq, lt
  not not_1 (Q, comparator_1_gt);
endmodule
